// Logisim project Circuits.circ as structural Verilog
module test (
  output out_1,
  output out_2
);

  wire clock_1_out;
  wire [2:0] counter_1_q, rom_1_data;

  Clock clock_1 (.out(clock_1_out));
  Counter #(.max('h7), .width(3)) counter_1 (
    .clk(clock_1_out), .Q(counter_1_q));  // open: clr, load, up, count, D, carry
  ROM #(.addrWidth(3), .dataWidth(3)) rom_1 (.addr(counter_1_q), .data(rom_1_data));
  FullAdder fulladder_1 (.A(rom_1_data[0]), .B(rom_1_data[1]), .Cin(rom_1_data[2]), .S(out_1), .Cout(out_2));

  // Notes on the sheet:
  //   contents of rom_1 (hex, n*v repeats v):
  //   0 1 2 3 4 5 6 7
endmodule

module FullAdder (
  input  A,
  input  B,
  input  Cin,
  output S,
  output Cout
);

  wire and_1_out, and_2_out, and_3_out, xor_1_out;

  and and_1 (and_1_out, A, B);
  and and_2 (and_2_out, A, Cin);
  and and_3 (and_3_out, B, Cin);
  xor xor_1 (xor_1_out, A, B);
  xor xor_2 (S, xor_1_out, Cin);
  or or_1 (Cout, and_1_out, and_2_out, and_3_out);
endmodule

module Adder_2_Bit (
  input  A1,
  input  A0,
  input  B1,
  input  B0,
  input  Cin,
  output Cout,
  output S1,
  output S0
);

  wire fulladder_1_cout;

  FullAdder fulladder_1 (.A(B0), .B(A0), .Cin(Cin), .S(S0), .Cout(fulladder_1_cout));
  FullAdder fulladder_2 (.A(B1), .B(A1), .Cin(fulladder_1_cout), .S(S1), .Cout(Cout));
endmodule

module Adder_4_Bit (
  input  A3,
  input  A2,
  input  A1,
  input  A0,
  input  B3,
  input  B2,
  input  B1,
  input  B0,
  input  Cin,
  output Cout,
  output S3,
  output S2,
  output S1,
  output S0
);

  wire adder_2_bit_1_cout;

  Adder_2_Bit adder_2_bit_1 (
    .A1(A1), .A0(A0), .B1(B1), .B0(B0), .Cin(Cin), .Cout(adder_2_bit_1_cout), .S1(S1), .S0(S0));
  Adder_2_Bit adder_2_bit_2 (
    .A1(A3), .A0(A2), .B1(B3), .B0(B2), .Cin(adder_2_bit_1_cout), .Cout(Cout), .S1(S3), .S0(S2));
endmodule

module Adder_8_Bit (
  input  A7,
  input  A6,
  input  A5,
  input  A4,
  input  A3,
  input  A2,
  input  A1,
  input  A0,
  input  B7,
  input  B6,
  input  B5,
  input  B4,
  input  B3,
  input  B2,
  input  B1,
  input  B0,
  input  Cin,
  output Cout,
  output S7,
  output S6,
  output S5,
  output S4,
  output S3,
  output S2,
  output S1,
  output S0
);

  wire adder_4_bit_1_cout;

  Adder_4_Bit adder_4_bit_1 (
    .A3(A3), .A2(A2), .A1(A1), .A0(A0), .B3(B3), .B2(B2), .B1(B1), .B0(B0), .Cin(Cin),
    .Cout(adder_4_bit_1_cout), .S3(S3), .S2(S2), .S1(S1), .S0(S0));
  Adder_4_Bit adder_4_bit_2 (
    .A3(A7), .A2(A6), .A1(A5), .A0(A4), .B3(B7), .B2(B6), .B1(B5), .B0(B4), .Cin(adder_4_bit_1_cout),
    .Cout(Cout), .S3(S7), .S2(S6), .S1(S5), .S0(S4));
endmodule

module Adder_8_Bit_Bus (
  input  [7:0] A,
  input  [7:0] B,
  input  Cin,
  output Cout,
  output [7:0] S
);

  Adder_8_Bit adder_8_bit_1 (
    .A7(A[7]), .A6(A[6]), .A5(A[5]), .A4(A[4]), .A3(A[3]), .A2(A[2]), .A1(A[1]), .A0(A[0]), .B7(B[7]),
    .B6(B[6]), .B5(B[5]), .B4(B[4]), .B3(B[3]), .B2(B[2]), .B1(B[1]), .B0(B[0]), .Cin(Cin), .Cout(Cout),
    .S7(S[7]), .S6(S[6]), .S5(S[5]), .S4(S[4]), .S3(S[3]), .S2(S[2]), .S1(S[1]), .S0(S[0]));
endmodule

module Adder_Tree_8_Bit (
  input  [7:0] A,
  input  [7:0] B,
  input  [7:0] C,
  input  [7:0] D,
  input  [7:0] E,
  input  [7:0] F,
  input  [7:0] G,
  input  [7:0] H,
  output [7:0] S
);

  wire [7:0] adder_8_bit_bus_1_s, adder_8_bit_bus_2_s, adder_8_bit_bus_3_s, adder_8_bit_bus_4_s,
       adder_8_bit_bus_5_s, adder_8_bit_bus_6_s;

  Adder_8_Bit_Bus adder_8_bit_bus_1 (.A(A), .B(B), .Cin(1'b0), .S(adder_8_bit_bus_1_s));  // open: Cout
  Adder_8_Bit_Bus adder_8_bit_bus_2 (.A(C), .B(D), .Cin(1'b0), .S(adder_8_bit_bus_2_s));  // open: Cout
  Adder_8_Bit_Bus adder_8_bit_bus_3 (.A(E), .B(F), .Cin(1'b0), .S(adder_8_bit_bus_3_s));  // open: Cout
  Adder_8_Bit_Bus adder_8_bit_bus_4 (.A(G), .B(H), .Cin(1'b0), .S(adder_8_bit_bus_4_s));  // open: Cout
  Adder_8_Bit_Bus adder_8_bit_bus_5 (
    .A(adder_8_bit_bus_1_s), .B(adder_8_bit_bus_2_s), .Cin(1'b0), .S(adder_8_bit_bus_5_s));  // open: Cout
  Adder_8_Bit_Bus adder_8_bit_bus_6 (
    .A(adder_8_bit_bus_3_s), .B(adder_8_bit_bus_4_s), .Cin(1'b0), .S(adder_8_bit_bus_6_s));  // open: Cout
  Adder_8_Bit_Bus adder_8_bit_bus_7 (
    .A(adder_8_bit_bus_5_s), .B(adder_8_bit_bus_6_s), .Cin(1'b0), .S(S));  // open: Cout
endmodule

module Weight_Multiplier (
  input  S,
  input  [7:0] W,
  output [7:0] P
);

  wire [7:0] bit_extender_1_out;

  assign bit_extender_1_out = {{7{S}}, S};  // Bit_Extender bit_extender_1
  assign P = bit_extender_1_out & W;  // AND_Gate and_1, 8 bits wide
endmodule

module Perceptron_0 (
  input  I_1,
  input  I_2,
  input  I_3,
  input  I_4,
  input  I_5,
  input  I_6,
  input  I_7,
  input  I_8,
  input  I_9,
  input  I_10,
  input  I_11,
  input  I_12,
  input  I_13,
  input  I_14,
  input  I_15,
  input  I_16,
  input  I_17,
  input  I_18,
  input  I_19,
  input  I_20,
  input  I_21,
  input  I_22,
  input  I_23,
  input  I_24,
  input  I_25,
  input  I_26,
  input  I_27,
  input  I_28,
  input  I_29,
  input  I_30,
  input  I_31,
  input  I_32,
  input  I_33,
  input  I_34,
  input  I_35,
  input  I_36,
  input  I_37,
  input  I_38,
  input  I_39,
  input  I_40,
  input  I_41,
  input  I_42,
  input  I_43,
  input  I_44,
  input  I_45,
  input  I_46,
  input  I_47,
  input  I_48,
  input  I_49,
  input  I_50,
  input  I_51,
  input  I_52,
  input  I_53,
  input  I_54,
  input  I_55,
  input  I_56,
  input  I_57,
  input  I_58,
  input  I_59,
  input  I_60,
  input  I_61,
  input  I_62,
  input  I_63,
  input  I_64,
  output [7:0] Score_0
);

  wire [7:0] adder_tree_8_bit_1_s, adder_tree_8_bit_2_s, adder_tree_8_bit_3_s, adder_tree_8_bit_4_s,
       adder_tree_8_bit_5_s, adder_tree_8_bit_6_s, adder_tree_8_bit_7_s, adder_tree_8_bit_8_s,
       adder_tree_8_bit_9_s, weight_multiplier_1_p, weight_multiplier_2_p, weight_multiplier_3_p,
       weight_multiplier_4_p, weight_multiplier_5_p, weight_multiplier_6_p, weight_multiplier_7_p,
       weight_multiplier_8_p, weight_multiplier_9_p, weight_multiplier_10_p, weight_multiplier_11_p,
       weight_multiplier_12_p, weight_multiplier_13_p, weight_multiplier_14_p, weight_multiplier_15_p,
       weight_multiplier_16_p, weight_multiplier_17_p, weight_multiplier_18_p, weight_multiplier_19_p,
       weight_multiplier_20_p, weight_multiplier_21_p, weight_multiplier_22_p, weight_multiplier_23_p,
       weight_multiplier_24_p, weight_multiplier_25_p, weight_multiplier_26_p, weight_multiplier_27_p,
       weight_multiplier_28_p, weight_multiplier_29_p, weight_multiplier_30_p, weight_multiplier_31_p,
       weight_multiplier_32_p, weight_multiplier_33_p, weight_multiplier_34_p, weight_multiplier_35_p,
       weight_multiplier_36_p, weight_multiplier_37_p, weight_multiplier_38_p, weight_multiplier_39_p,
       weight_multiplier_40_p, weight_multiplier_41_p, weight_multiplier_42_p, weight_multiplier_43_p,
       weight_multiplier_44_p, weight_multiplier_45_p, weight_multiplier_46_p, weight_multiplier_47_p,
       weight_multiplier_48_p, weight_multiplier_49_p, weight_multiplier_50_p, weight_multiplier_51_p,
       weight_multiplier_52_p, weight_multiplier_53_p, weight_multiplier_54_p, weight_multiplier_55_p,
       weight_multiplier_56_p, weight_multiplier_57_p, weight_multiplier_58_p, weight_multiplier_59_p,
       weight_multiplier_60_p, weight_multiplier_61_p, weight_multiplier_62_p, weight_multiplier_63_p,
       weight_multiplier_64_p;

  Weight_Multiplier weight_multiplier_1 (.S(I_1), .W({8{1'b0}}), .P(weight_multiplier_1_p));
  Weight_Multiplier weight_multiplier_2 (.S(I_2), .W({8{1'b1}}), .P(weight_multiplier_2_p));
  Weight_Multiplier weight_multiplier_3 (.S(I_3), .W({8{1'b0}}), .P(weight_multiplier_3_p));
  Weight_Multiplier weight_multiplier_4 (.S(I_4), .W(8'h1), .P(weight_multiplier_4_p));
  Weight_Multiplier weight_multiplier_5 (.S(I_5), .W({8{1'b0}}), .P(weight_multiplier_5_p));
  Weight_Multiplier weight_multiplier_6 (.S(I_6), .W(8'hfe), .P(weight_multiplier_6_p));
  Weight_Multiplier weight_multiplier_7 (.S(I_7), .W(8'hfe), .P(weight_multiplier_7_p));
  Weight_Multiplier weight_multiplier_8 (.S(I_8), .W({8{1'b1}}), .P(weight_multiplier_8_p));
  Weight_Multiplier weight_multiplier_9 (.S(I_9), .W({8{1'b0}}), .P(weight_multiplier_9_p));
  Weight_Multiplier weight_multiplier_10 (.S(I_10), .W({8{1'b1}}), .P(weight_multiplier_10_p));
  Weight_Multiplier weight_multiplier_11 (.S(I_11), .W({8{1'b0}}), .P(weight_multiplier_11_p));
  Weight_Multiplier weight_multiplier_12 (.S(I_12), .W({8{1'b0}}), .P(weight_multiplier_12_p));
  Weight_Multiplier weight_multiplier_13 (.S(I_13), .W({8{1'b0}}), .P(weight_multiplier_13_p));
  Weight_Multiplier weight_multiplier_14 (.S(I_14), .W(8'h1), .P(weight_multiplier_14_p));
  Weight_Multiplier weight_multiplier_15 (.S(I_15), .W(8'hfe), .P(weight_multiplier_15_p));
  Weight_Multiplier weight_multiplier_16 (.S(I_16), .W(8'hfe), .P(weight_multiplier_16_p));
  Weight_Multiplier weight_multiplier_17 (.S(I_17), .W({8{1'b0}}), .P(weight_multiplier_17_p));
  Weight_Multiplier weight_multiplier_18 (.S(I_18), .W(8'hfe), .P(weight_multiplier_18_p));
  Weight_Multiplier weight_multiplier_19 (.S(I_19), .W(8'h2), .P(weight_multiplier_19_p));
  Weight_Multiplier weight_multiplier_20 (.S(I_20), .W({8{1'b0}}), .P(weight_multiplier_20_p));
  Weight_Multiplier weight_multiplier_21 (.S(I_21), .W(8'hfd), .P(weight_multiplier_21_p));
  Weight_Multiplier weight_multiplier_22 (.S(I_22), .W(8'h2), .P(weight_multiplier_22_p));
  Weight_Multiplier weight_multiplier_23 (.S(I_23), .W(8'h1), .P(weight_multiplier_23_p));
  Weight_Multiplier weight_multiplier_24 (.S(I_24), .W({8{1'b1}}), .P(weight_multiplier_24_p));
  Weight_Multiplier weight_multiplier_25 (.S(I_25), .W({8{1'b0}}), .P(weight_multiplier_25_p));
  Weight_Multiplier weight_multiplier_26 (.S(I_26), .W(8'h2), .P(weight_multiplier_26_p));
  Weight_Multiplier weight_multiplier_27 (.S(I_27), .W(8'h2), .P(weight_multiplier_27_p));
  Weight_Multiplier weight_multiplier_28 (.S(I_28), .W(8'hfe), .P(weight_multiplier_28_p));
  Weight_Multiplier weight_multiplier_29 (.S(I_29), .W(8'hfd), .P(weight_multiplier_29_p));
  Weight_Multiplier weight_multiplier_30 (.S(I_30), .W(8'h1), .P(weight_multiplier_30_p));
  Weight_Multiplier weight_multiplier_31 (.S(I_31), .W(8'h2), .P(weight_multiplier_31_p));
  Weight_Multiplier weight_multiplier_32 (.S(I_32), .W({8{1'b0}}), .P(weight_multiplier_32_p));
  Weight_Multiplier weight_multiplier_33 (.S(I_33), .W({8{1'b0}}), .P(weight_multiplier_33_p));
  Weight_Multiplier weight_multiplier_34 (.S(I_34), .W(8'h1), .P(weight_multiplier_34_p));
  Weight_Multiplier weight_multiplier_35 (.S(I_35), .W(8'h2), .P(weight_multiplier_35_p));
  Weight_Multiplier weight_multiplier_36 (.S(I_36), .W(8'hfe), .P(weight_multiplier_36_p));
  Weight_Multiplier weight_multiplier_37 (.S(I_37), .W(8'hfe), .P(weight_multiplier_37_p));
  Weight_Multiplier weight_multiplier_38 (.S(I_38), .W({8{1'b0}}), .P(weight_multiplier_38_p));
  Weight_Multiplier weight_multiplier_39 (.S(I_39), .W(8'h2), .P(weight_multiplier_39_p));
  Weight_Multiplier weight_multiplier_40 (.S(I_40), .W({8{1'b0}}), .P(weight_multiplier_40_p));
  Weight_Multiplier weight_multiplier_41 (.S(I_41), .W({8{1'b0}}), .P(weight_multiplier_41_p));
  Weight_Multiplier weight_multiplier_42 (.S(I_42), .W(8'hfe), .P(weight_multiplier_42_p));
  Weight_Multiplier weight_multiplier_43 (.S(I_43), .W(8'h3), .P(weight_multiplier_43_p));
  Weight_Multiplier weight_multiplier_44 (.S(I_44), .W({8{1'b1}}), .P(weight_multiplier_44_p));
  Weight_Multiplier weight_multiplier_45 (.S(I_45), .W(8'hfe), .P(weight_multiplier_45_p));
  Weight_Multiplier weight_multiplier_46 (.S(I_46), .W(8'h1), .P(weight_multiplier_46_p));
  Weight_Multiplier weight_multiplier_47 (.S(I_47), .W(8'h1), .P(weight_multiplier_47_p));
  Weight_Multiplier weight_multiplier_48 (.S(I_48), .W({8{1'b0}}), .P(weight_multiplier_48_p));
  Weight_Multiplier weight_multiplier_49 (.S(I_49), .W(8'hfe), .P(weight_multiplier_49_p));
  Weight_Multiplier weight_multiplier_50 (.S(I_50), .W(8'hfd), .P(weight_multiplier_50_p));
  Weight_Multiplier weight_multiplier_51 (.S(I_51), .W(8'h2), .P(weight_multiplier_51_p));
  Weight_Multiplier weight_multiplier_52 (.S(I_52), .W({8{1'b1}}), .P(weight_multiplier_52_p));
  Weight_Multiplier weight_multiplier_53 (.S(I_53), .W(8'h1), .P(weight_multiplier_53_p));
  Weight_Multiplier weight_multiplier_54 (.S(I_54), .W(8'h2), .P(weight_multiplier_54_p));
  Weight_Multiplier weight_multiplier_55 (.S(I_55), .W(8'hfe), .P(weight_multiplier_55_p));
  Weight_Multiplier weight_multiplier_56 (.S(I_56), .W({8{1'b1}}), .P(weight_multiplier_56_p));
  Weight_Multiplier weight_multiplier_57 (.S(I_57), .W({8{1'b0}}), .P(weight_multiplier_57_p));
  Weight_Multiplier weight_multiplier_58 (.S(I_58), .W({8{1'b1}}), .P(weight_multiplier_58_p));
  Weight_Multiplier weight_multiplier_59 (.S(I_59), .W({8{1'b1}}), .P(weight_multiplier_59_p));
  Weight_Multiplier weight_multiplier_60 (.S(I_60), .W(8'h1), .P(weight_multiplier_60_p));
  Weight_Multiplier weight_multiplier_61 (.S(I_61), .W({8{1'b0}}), .P(weight_multiplier_61_p));
  Weight_Multiplier weight_multiplier_62 (.S(I_62), .W({8{1'b1}}), .P(weight_multiplier_62_p));
  Weight_Multiplier weight_multiplier_63 (.S(I_63), .W(8'hfe), .P(weight_multiplier_63_p));
  Weight_Multiplier weight_multiplier_64 (.S(I_64), .W(8'hfe), .P(weight_multiplier_64_p));
  Adder_Tree_8_Bit adder_tree_8_bit_1 (
    .A(weight_multiplier_1_p), .B(weight_multiplier_2_p), .C(weight_multiplier_3_p),
    .D(weight_multiplier_4_p), .E(weight_multiplier_5_p), .F(weight_multiplier_6_p),
    .G(weight_multiplier_7_p), .H(weight_multiplier_8_p), .S(adder_tree_8_bit_1_s));
  Adder_Tree_8_Bit adder_tree_8_bit_2 (
    .A(weight_multiplier_9_p), .B(weight_multiplier_10_p), .C(weight_multiplier_11_p),
    .D(weight_multiplier_12_p), .E(weight_multiplier_13_p), .F(weight_multiplier_14_p),
    .G(weight_multiplier_15_p), .H(weight_multiplier_16_p), .S(adder_tree_8_bit_2_s));
  Adder_Tree_8_Bit adder_tree_8_bit_3 (
    .A(weight_multiplier_17_p), .B(weight_multiplier_18_p), .C(weight_multiplier_19_p),
    .D(weight_multiplier_20_p), .E(weight_multiplier_21_p), .F(weight_multiplier_22_p),
    .G(weight_multiplier_23_p), .H(weight_multiplier_24_p), .S(adder_tree_8_bit_3_s));
  Adder_Tree_8_Bit adder_tree_8_bit_4 (
    .A(weight_multiplier_25_p), .B(weight_multiplier_26_p), .C(weight_multiplier_27_p),
    .D(weight_multiplier_28_p), .E(weight_multiplier_29_p), .F(weight_multiplier_30_p),
    .G(weight_multiplier_31_p), .H(weight_multiplier_32_p), .S(adder_tree_8_bit_4_s));
  Adder_Tree_8_Bit adder_tree_8_bit_5 (
    .A(weight_multiplier_33_p), .B(weight_multiplier_34_p), .C(weight_multiplier_35_p),
    .D(weight_multiplier_36_p), .E(weight_multiplier_37_p), .F(weight_multiplier_38_p),
    .G(weight_multiplier_39_p), .H(weight_multiplier_40_p), .S(adder_tree_8_bit_5_s));
  Adder_Tree_8_Bit adder_tree_8_bit_6 (
    .A(weight_multiplier_41_p), .B(weight_multiplier_42_p), .C(weight_multiplier_43_p),
    .D(weight_multiplier_44_p), .E(weight_multiplier_45_p), .F(weight_multiplier_46_p),
    .G(weight_multiplier_47_p), .H(weight_multiplier_48_p), .S(adder_tree_8_bit_6_s));
  Adder_Tree_8_Bit adder_tree_8_bit_7 (
    .A(weight_multiplier_49_p), .B(weight_multiplier_50_p), .C(weight_multiplier_51_p),
    .D(weight_multiplier_52_p), .E(weight_multiplier_53_p), .F(weight_multiplier_54_p),
    .G(weight_multiplier_55_p), .H(weight_multiplier_56_p), .S(adder_tree_8_bit_7_s));
  Adder_Tree_8_Bit adder_tree_8_bit_8 (
    .A(weight_multiplier_57_p), .B(weight_multiplier_58_p), .C(weight_multiplier_59_p),
    .D(weight_multiplier_60_p), .E(weight_multiplier_61_p), .F(weight_multiplier_62_p),
    .G(weight_multiplier_63_p), .H(weight_multiplier_64_p), .S(adder_tree_8_bit_8_s));
  Adder_Tree_8_Bit adder_tree_8_bit_9 (
    .A(adder_tree_8_bit_1_s), .B(adder_tree_8_bit_2_s), .C(adder_tree_8_bit_3_s), .D(adder_tree_8_bit_4_s),
    .E(adder_tree_8_bit_5_s), .F(adder_tree_8_bit_6_s), .G(adder_tree_8_bit_7_s), .H(adder_tree_8_bit_8_s),
    .S(adder_tree_8_bit_9_s));
  Adder_8_Bit_Bus adder_8_bit_bus_1 (.A(adder_tree_8_bit_9_s), .B({8{1'b1}}), .Cin(1'b0), .S(Score_0));  // open: Cout
endmodule

module Perceptron_1 (
  input  I_1,
  input  I_2,
  input  I_3,
  input  I_4,
  input  I_5,
  input  I_6,
  input  I_7,
  input  I_8,
  input  I_9,
  input  I_10,
  input  I_11,
  input  I_12,
  input  I_13,
  input  I_14,
  input  I_15,
  input  I_16,
  input  I_17,
  input  I_18,
  input  I_19,
  input  I_20,
  input  I_21,
  input  I_22,
  input  I_23,
  input  I_24,
  input  I_25,
  input  I_26,
  input  I_27,
  input  I_28,
  input  I_29,
  input  I_30,
  input  I_31,
  input  I_32,
  input  I_33,
  input  I_34,
  input  I_35,
  input  I_36,
  input  I_37,
  input  I_38,
  input  I_39,
  input  I_40,
  input  I_41,
  input  I_42,
  input  I_43,
  input  I_44,
  input  I_45,
  input  I_46,
  input  I_47,
  input  I_48,
  input  I_49,
  input  I_50,
  input  I_51,
  input  I_52,
  input  I_53,
  input  I_54,
  input  I_55,
  input  I_56,
  input  I_57,
  input  I_58,
  input  I_59,
  input  I_60,
  input  I_61,
  input  I_62,
  input  I_63,
  input  I_64,
  output [7:0] Score_1
);

  wire [7:0] adder_tree_8_bit_1_s, adder_tree_8_bit_2_s, adder_tree_8_bit_3_s, adder_tree_8_bit_4_s,
       adder_tree_8_bit_5_s, adder_tree_8_bit_6_s, adder_tree_8_bit_7_s, adder_tree_8_bit_8_s,
       adder_tree_8_bit_9_s, weight_multiplier_1_p, weight_multiplier_2_p, weight_multiplier_3_p,
       weight_multiplier_4_p, weight_multiplier_5_p, weight_multiplier_6_p, weight_multiplier_7_p,
       weight_multiplier_8_p, weight_multiplier_9_p, weight_multiplier_10_p, weight_multiplier_11_p,
       weight_multiplier_12_p, weight_multiplier_13_p, weight_multiplier_14_p, weight_multiplier_15_p,
       weight_multiplier_16_p, weight_multiplier_17_p, weight_multiplier_18_p, weight_multiplier_19_p,
       weight_multiplier_20_p, weight_multiplier_21_p, weight_multiplier_22_p, weight_multiplier_23_p,
       weight_multiplier_24_p, weight_multiplier_25_p, weight_multiplier_26_p, weight_multiplier_27_p,
       weight_multiplier_28_p, weight_multiplier_29_p, weight_multiplier_30_p, weight_multiplier_31_p,
       weight_multiplier_32_p, weight_multiplier_33_p, weight_multiplier_34_p, weight_multiplier_35_p,
       weight_multiplier_36_p, weight_multiplier_37_p, weight_multiplier_38_p, weight_multiplier_39_p,
       weight_multiplier_40_p, weight_multiplier_41_p, weight_multiplier_42_p, weight_multiplier_43_p,
       weight_multiplier_44_p, weight_multiplier_45_p, weight_multiplier_46_p, weight_multiplier_47_p,
       weight_multiplier_48_p, weight_multiplier_49_p, weight_multiplier_50_p, weight_multiplier_51_p,
       weight_multiplier_52_p, weight_multiplier_53_p, weight_multiplier_54_p, weight_multiplier_55_p,
       weight_multiplier_56_p, weight_multiplier_57_p, weight_multiplier_58_p, weight_multiplier_59_p,
       weight_multiplier_60_p, weight_multiplier_61_p, weight_multiplier_62_p, weight_multiplier_63_p,
       weight_multiplier_64_p;

  Weight_Multiplier weight_multiplier_1 (.S(I_1), .W({8{1'b0}}), .P(weight_multiplier_1_p));
  Weight_Multiplier weight_multiplier_2 (.S(I_2), .W({8{1'b1}}), .P(weight_multiplier_2_p));
  Weight_Multiplier weight_multiplier_3 (.S(I_3), .W({8{1'b1}}), .P(weight_multiplier_3_p));
  Weight_Multiplier weight_multiplier_4 (.S(I_4), .W({8{1'b0}}), .P(weight_multiplier_4_p));
  Weight_Multiplier weight_multiplier_5 (.S(I_5), .W(8'hfd), .P(weight_multiplier_5_p));
  Weight_Multiplier weight_multiplier_6 (.S(I_6), .W(8'h2), .P(weight_multiplier_6_p));
  Weight_Multiplier weight_multiplier_7 (.S(I_7), .W(8'h1), .P(weight_multiplier_7_p));
  Weight_Multiplier weight_multiplier_8 (.S(I_8), .W(8'hfe), .P(weight_multiplier_8_p));
  Weight_Multiplier weight_multiplier_9 (.S(I_9), .W({8{1'b0}}), .P(weight_multiplier_9_p));
  Weight_Multiplier weight_multiplier_10 (.S(I_10), .W(8'hfc), .P(weight_multiplier_10_p));
  Weight_Multiplier weight_multiplier_11 (.S(I_11), .W(8'hfe), .P(weight_multiplier_11_p));
  Weight_Multiplier weight_multiplier_12 (.S(I_12), .W(8'hfe), .P(weight_multiplier_12_p));
  Weight_Multiplier weight_multiplier_13 (.S(I_13), .W({8{1'b0}}), .P(weight_multiplier_13_p));
  Weight_Multiplier weight_multiplier_14 (.S(I_14), .W({8{1'b0}}), .P(weight_multiplier_14_p));
  Weight_Multiplier weight_multiplier_15 (.S(I_15), .W(8'hfe), .P(weight_multiplier_15_p));
  Weight_Multiplier weight_multiplier_16 (.S(I_16), .W(8'hfe), .P(weight_multiplier_16_p));
  Weight_Multiplier weight_multiplier_17 (.S(I_17), .W({8{1'b0}}), .P(weight_multiplier_17_p));
  Weight_Multiplier weight_multiplier_18 (.S(I_18), .W({8{1'b1}}), .P(weight_multiplier_18_p));
  Weight_Multiplier weight_multiplier_19 (.S(I_19), .W({8{1'b1}}), .P(weight_multiplier_19_p));
  Weight_Multiplier weight_multiplier_20 (.S(I_20), .W(8'h3), .P(weight_multiplier_20_p));
  Weight_Multiplier weight_multiplier_21 (.S(I_21), .W(8'h3), .P(weight_multiplier_21_p));
  Weight_Multiplier weight_multiplier_22 (.S(I_22), .W({8{1'b1}}), .P(weight_multiplier_22_p));
  Weight_Multiplier weight_multiplier_23 (.S(I_23), .W(8'h1), .P(weight_multiplier_23_p));
  Weight_Multiplier weight_multiplier_24 (.S(I_24), .W(8'hfe), .P(weight_multiplier_24_p));
  Weight_Multiplier weight_multiplier_25 (.S(I_25), .W({8{1'b0}}), .P(weight_multiplier_25_p));
  Weight_Multiplier weight_multiplier_26 (.S(I_26), .W(8'h2), .P(weight_multiplier_26_p));
  Weight_Multiplier weight_multiplier_27 (.S(I_27), .W(8'h3), .P(weight_multiplier_27_p));
  Weight_Multiplier weight_multiplier_28 (.S(I_28), .W(8'h2), .P(weight_multiplier_28_p));
  Weight_Multiplier weight_multiplier_29 (.S(I_29), .W(8'h2), .P(weight_multiplier_29_p));
  Weight_Multiplier weight_multiplier_30 (.S(I_30), .W({8{1'b0}}), .P(weight_multiplier_30_p));
  Weight_Multiplier weight_multiplier_31 (.S(I_31), .W({8{1'b1}}), .P(weight_multiplier_31_p));
  Weight_Multiplier weight_multiplier_32 (.S(I_32), .W({8{1'b0}}), .P(weight_multiplier_32_p));
  Weight_Multiplier weight_multiplier_33 (.S(I_33), .W({8{1'b0}}), .P(weight_multiplier_33_p));
  Weight_Multiplier weight_multiplier_34 (.S(I_34), .W({8{1'b1}}), .P(weight_multiplier_34_p));
  Weight_Multiplier weight_multiplier_35 (.S(I_35), .W({8{1'b0}}), .P(weight_multiplier_35_p));
  Weight_Multiplier weight_multiplier_36 (.S(I_36), .W({8{1'b1}}), .P(weight_multiplier_36_p));
  Weight_Multiplier weight_multiplier_37 (.S(I_37), .W(8'h1), .P(weight_multiplier_37_p));
  Weight_Multiplier weight_multiplier_38 (.S(I_38), .W({8{1'b1}}), .P(weight_multiplier_38_p));
  Weight_Multiplier weight_multiplier_39 (.S(I_39), .W({8{1'b1}}), .P(weight_multiplier_39_p));
  Weight_Multiplier weight_multiplier_40 (.S(I_40), .W({8{1'b0}}), .P(weight_multiplier_40_p));
  Weight_Multiplier weight_multiplier_41 (.S(I_41), .W({8{1'b0}}), .P(weight_multiplier_41_p));
  Weight_Multiplier weight_multiplier_42 (.S(I_42), .W(8'hfc), .P(weight_multiplier_42_p));
  Weight_Multiplier weight_multiplier_43 (.S(I_43), .W({8{1'b0}}), .P(weight_multiplier_43_p));
  Weight_Multiplier weight_multiplier_44 (.S(I_44), .W(8'h2), .P(weight_multiplier_44_p));
  Weight_Multiplier weight_multiplier_45 (.S(I_45), .W(8'h2), .P(weight_multiplier_45_p));
  Weight_Multiplier weight_multiplier_46 (.S(I_46), .W(8'hfe), .P(weight_multiplier_46_p));
  Weight_Multiplier weight_multiplier_47 (.S(I_47), .W(8'hfe), .P(weight_multiplier_47_p));
  Weight_Multiplier weight_multiplier_48 (.S(I_48), .W({8{1'b0}}), .P(weight_multiplier_48_p));
  Weight_Multiplier weight_multiplier_49 (.S(I_49), .W({8{1'b1}}), .P(weight_multiplier_49_p));
  Weight_Multiplier weight_multiplier_50 (.S(I_50), .W(8'hfc), .P(weight_multiplier_50_p));
  Weight_Multiplier weight_multiplier_51 (.S(I_51), .W({8{1'b1}}), .P(weight_multiplier_51_p));
  Weight_Multiplier weight_multiplier_52 (.S(I_52), .W({8{1'b0}}), .P(weight_multiplier_52_p));
  Weight_Multiplier weight_multiplier_53 (.S(I_53), .W(8'h2), .P(weight_multiplier_53_p));
  Weight_Multiplier weight_multiplier_54 (.S(I_54), .W(8'h1), .P(weight_multiplier_54_p));
  Weight_Multiplier weight_multiplier_55 (.S(I_55), .W({8{1'b1}}), .P(weight_multiplier_55_p));
  Weight_Multiplier weight_multiplier_56 (.S(I_56), .W(8'h2), .P(weight_multiplier_56_p));
  Weight_Multiplier weight_multiplier_57 (.S(I_57), .W({8{1'b0}}), .P(weight_multiplier_57_p));
  Weight_Multiplier weight_multiplier_58 (.S(I_58), .W(8'hfe), .P(weight_multiplier_58_p));
  Weight_Multiplier weight_multiplier_59 (.S(I_59), .W({8{1'b1}}), .P(weight_multiplier_59_p));
  Weight_Multiplier weight_multiplier_60 (.S(I_60), .W({8{1'b0}}), .P(weight_multiplier_60_p));
  Weight_Multiplier weight_multiplier_61 (.S(I_61), .W(8'h1), .P(weight_multiplier_61_p));
  Weight_Multiplier weight_multiplier_62 (.S(I_62), .W(8'h2), .P(weight_multiplier_62_p));
  Weight_Multiplier weight_multiplier_63 (.S(I_63), .W(8'h2), .P(weight_multiplier_63_p));
  Weight_Multiplier weight_multiplier_64 (.S(I_64), .W(8'h3), .P(weight_multiplier_64_p));
  Adder_Tree_8_Bit adder_tree_8_bit_1 (
    .A(weight_multiplier_1_p), .B(weight_multiplier_2_p), .C(weight_multiplier_3_p),
    .D(weight_multiplier_4_p), .E(weight_multiplier_5_p), .F(weight_multiplier_6_p),
    .G(weight_multiplier_7_p), .H(weight_multiplier_8_p), .S(adder_tree_8_bit_1_s));
  Adder_Tree_8_Bit adder_tree_8_bit_2 (
    .A(weight_multiplier_9_p), .B(weight_multiplier_10_p), .C(weight_multiplier_11_p),
    .D(weight_multiplier_12_p), .E(weight_multiplier_13_p), .F(weight_multiplier_14_p),
    .G(weight_multiplier_15_p), .H(weight_multiplier_16_p), .S(adder_tree_8_bit_2_s));
  Adder_Tree_8_Bit adder_tree_8_bit_3 (
    .A(weight_multiplier_17_p), .B(weight_multiplier_18_p), .C(weight_multiplier_19_p),
    .D(weight_multiplier_20_p), .E(weight_multiplier_21_p), .F(weight_multiplier_22_p),
    .G(weight_multiplier_23_p), .H(weight_multiplier_24_p), .S(adder_tree_8_bit_3_s));
  Adder_Tree_8_Bit adder_tree_8_bit_4 (
    .A(weight_multiplier_25_p), .B(weight_multiplier_26_p), .C(weight_multiplier_27_p),
    .D(weight_multiplier_28_p), .E(weight_multiplier_29_p), .F(weight_multiplier_30_p),
    .G(weight_multiplier_31_p), .H(weight_multiplier_32_p), .S(adder_tree_8_bit_4_s));
  Adder_Tree_8_Bit adder_tree_8_bit_5 (
    .A(weight_multiplier_33_p), .B(weight_multiplier_34_p), .C(weight_multiplier_35_p),
    .D(weight_multiplier_36_p), .E(weight_multiplier_37_p), .F(weight_multiplier_38_p),
    .G(weight_multiplier_39_p), .H(weight_multiplier_40_p), .S(adder_tree_8_bit_5_s));
  Adder_Tree_8_Bit adder_tree_8_bit_6 (
    .A(weight_multiplier_41_p), .B(weight_multiplier_42_p), .C(weight_multiplier_43_p),
    .D(weight_multiplier_44_p), .E(weight_multiplier_45_p), .F(weight_multiplier_46_p),
    .G(weight_multiplier_47_p), .H(weight_multiplier_48_p), .S(adder_tree_8_bit_6_s));
  Adder_Tree_8_Bit adder_tree_8_bit_7 (
    .A(weight_multiplier_49_p), .B(weight_multiplier_50_p), .C(weight_multiplier_51_p),
    .D(weight_multiplier_52_p), .E(weight_multiplier_53_p), .F(weight_multiplier_54_p),
    .G(weight_multiplier_55_p), .H(weight_multiplier_56_p), .S(adder_tree_8_bit_7_s));
  Adder_Tree_8_Bit adder_tree_8_bit_8 (
    .A(weight_multiplier_57_p), .B(weight_multiplier_58_p), .C(weight_multiplier_59_p),
    .D(weight_multiplier_60_p), .E(weight_multiplier_61_p), .F(weight_multiplier_62_p),
    .G(weight_multiplier_63_p), .H(weight_multiplier_64_p), .S(adder_tree_8_bit_8_s));
  Adder_Tree_8_Bit adder_tree_8_bit_9 (
    .A(adder_tree_8_bit_1_s), .B(adder_tree_8_bit_2_s), .C(adder_tree_8_bit_3_s), .D(adder_tree_8_bit_4_s),
    .E(adder_tree_8_bit_5_s), .F(adder_tree_8_bit_6_s), .G(adder_tree_8_bit_7_s), .H(adder_tree_8_bit_8_s),
    .S(adder_tree_8_bit_9_s));
  Adder_8_Bit_Bus adder_8_bit_bus_1 (.A(adder_tree_8_bit_9_s), .B({8{1'b0}}), .Cin(1'b0), .S(Score_1));  // open: Cout
endmodule

module Perceptron_2 (
  input  I_1,
  input  I_2,
  input  I_3,
  input  I_4,
  input  I_5,
  input  I_6,
  input  I_7,
  input  I_8,
  input  I_9,
  input  I_10,
  input  I_11,
  input  I_12,
  input  I_13,
  input  I_14,
  input  I_15,
  input  I_16,
  input  I_17,
  input  I_18,
  input  I_19,
  input  I_20,
  input  I_21,
  input  I_22,
  input  I_23,
  input  I_24,
  input  I_25,
  input  I_26,
  input  I_27,
  input  I_28,
  input  I_29,
  input  I_30,
  input  I_31,
  input  I_32,
  input  I_33,
  input  I_34,
  input  I_35,
  input  I_36,
  input  I_37,
  input  I_38,
  input  I_39,
  input  I_40,
  input  I_41,
  input  I_42,
  input  I_43,
  input  I_44,
  input  I_45,
  input  I_46,
  input  I_47,
  input  I_48,
  input  I_49,
  input  I_50,
  input  I_51,
  input  I_52,
  input  I_53,
  input  I_54,
  input  I_55,
  input  I_56,
  input  I_57,
  input  I_58,
  input  I_59,
  input  I_60,
  input  I_61,
  input  I_62,
  input  I_63,
  input  I_64,
  output [7:0] Score_2
);

  wire [7:0] adder_tree_8_bit_1_s, adder_tree_8_bit_2_s, adder_tree_8_bit_3_s, adder_tree_8_bit_4_s,
       adder_tree_8_bit_5_s, adder_tree_8_bit_6_s, adder_tree_8_bit_7_s, adder_tree_8_bit_8_s,
       adder_tree_8_bit_9_s, weight_multiplier_1_p, weight_multiplier_2_p, weight_multiplier_3_p,
       weight_multiplier_4_p, weight_multiplier_5_p, weight_multiplier_6_p, weight_multiplier_7_p,
       weight_multiplier_8_p, weight_multiplier_9_p, weight_multiplier_10_p, weight_multiplier_11_p,
       weight_multiplier_12_p, weight_multiplier_13_p, weight_multiplier_14_p, weight_multiplier_15_p,
       weight_multiplier_16_p, weight_multiplier_17_p, weight_multiplier_18_p, weight_multiplier_19_p,
       weight_multiplier_20_p, weight_multiplier_21_p, weight_multiplier_22_p, weight_multiplier_23_p,
       weight_multiplier_24_p, weight_multiplier_25_p, weight_multiplier_26_p, weight_multiplier_27_p,
       weight_multiplier_28_p, weight_multiplier_29_p, weight_multiplier_30_p, weight_multiplier_31_p,
       weight_multiplier_32_p, weight_multiplier_33_p, weight_multiplier_34_p, weight_multiplier_35_p,
       weight_multiplier_36_p, weight_multiplier_37_p, weight_multiplier_38_p, weight_multiplier_39_p,
       weight_multiplier_40_p, weight_multiplier_41_p, weight_multiplier_42_p, weight_multiplier_43_p,
       weight_multiplier_44_p, weight_multiplier_45_p, weight_multiplier_46_p, weight_multiplier_47_p,
       weight_multiplier_48_p, weight_multiplier_49_p, weight_multiplier_50_p, weight_multiplier_51_p,
       weight_multiplier_52_p, weight_multiplier_53_p, weight_multiplier_54_p, weight_multiplier_55_p,
       weight_multiplier_56_p, weight_multiplier_57_p, weight_multiplier_58_p, weight_multiplier_59_p,
       weight_multiplier_60_p, weight_multiplier_61_p, weight_multiplier_62_p, weight_multiplier_63_p,
       weight_multiplier_64_p;

  Weight_Multiplier weight_multiplier_1 (.S(I_1), .W({8{1'b0}}), .P(weight_multiplier_1_p));
  Weight_Multiplier weight_multiplier_2 (.S(I_2), .W(8'hfe), .P(weight_multiplier_2_p));
  Weight_Multiplier weight_multiplier_3 (.S(I_3), .W(8'h1), .P(weight_multiplier_3_p));
  Weight_Multiplier weight_multiplier_4 (.S(I_4), .W({8{1'b0}}), .P(weight_multiplier_4_p));
  Weight_Multiplier weight_multiplier_5 (.S(I_5), .W({8{1'b0}}), .P(weight_multiplier_5_p));
  Weight_Multiplier weight_multiplier_6 (.S(I_6), .W({8{1'b1}}), .P(weight_multiplier_6_p));
  Weight_Multiplier weight_multiplier_7 (.S(I_7), .W(8'hfd), .P(weight_multiplier_7_p));
  Weight_Multiplier weight_multiplier_8 (.S(I_8), .W({8{1'b1}}), .P(weight_multiplier_8_p));
  Weight_Multiplier weight_multiplier_9 (.S(I_9), .W({8{1'b0}}), .P(weight_multiplier_9_p));
  Weight_Multiplier weight_multiplier_10 (.S(I_10), .W(8'h2), .P(weight_multiplier_10_p));
  Weight_Multiplier weight_multiplier_11 (.S(I_11), .W(8'h1), .P(weight_multiplier_11_p));
  Weight_Multiplier weight_multiplier_12 (.S(I_12), .W({8{1'b0}}), .P(weight_multiplier_12_p));
  Weight_Multiplier weight_multiplier_13 (.S(I_13), .W(8'h2), .P(weight_multiplier_13_p));
  Weight_Multiplier weight_multiplier_14 (.S(I_14), .W({8{1'b0}}), .P(weight_multiplier_14_p));
  Weight_Multiplier weight_multiplier_15 (.S(I_15), .W(8'h1), .P(weight_multiplier_15_p));
  Weight_Multiplier weight_multiplier_16 (.S(I_16), .W({8{1'b1}}), .P(weight_multiplier_16_p));
  Weight_Multiplier weight_multiplier_17 (.S(I_17), .W({8{1'b0}}), .P(weight_multiplier_17_p));
  Weight_Multiplier weight_multiplier_18 (.S(I_18), .W(8'h2), .P(weight_multiplier_18_p));
  Weight_Multiplier weight_multiplier_19 (.S(I_19), .W({8{1'b0}}), .P(weight_multiplier_19_p));
  Weight_Multiplier weight_multiplier_20 (.S(I_20), .W(8'hfd), .P(weight_multiplier_20_p));
  Weight_Multiplier weight_multiplier_21 (.S(I_21), .W(8'h2), .P(weight_multiplier_21_p));
  Weight_Multiplier weight_multiplier_22 (.S(I_22), .W({8{1'b0}}), .P(weight_multiplier_22_p));
  Weight_Multiplier weight_multiplier_23 (.S(I_23), .W(8'h2), .P(weight_multiplier_23_p));
  Weight_Multiplier weight_multiplier_24 (.S(I_24), .W({8{1'b1}}), .P(weight_multiplier_24_p));
  Weight_Multiplier weight_multiplier_25 (.S(I_25), .W({8{1'b0}}), .P(weight_multiplier_25_p));
  Weight_Multiplier weight_multiplier_26 (.S(I_26), .W(8'hfe), .P(weight_multiplier_26_p));
  Weight_Multiplier weight_multiplier_27 (.S(I_27), .W(8'hfd), .P(weight_multiplier_27_p));
  Weight_Multiplier weight_multiplier_28 (.S(I_28), .W(8'hfc), .P(weight_multiplier_28_p));
  Weight_Multiplier weight_multiplier_29 (.S(I_29), .W({8{1'b0}}), .P(weight_multiplier_29_p));
  Weight_Multiplier weight_multiplier_30 (.S(I_30), .W({8{1'b0}}), .P(weight_multiplier_30_p));
  Weight_Multiplier weight_multiplier_31 (.S(I_31), .W({8{1'b1}}), .P(weight_multiplier_31_p));
  Weight_Multiplier weight_multiplier_32 (.S(I_32), .W({8{1'b0}}), .P(weight_multiplier_32_p));
  Weight_Multiplier weight_multiplier_33 (.S(I_33), .W({8{1'b0}}), .P(weight_multiplier_33_p));
  Weight_Multiplier weight_multiplier_34 (.S(I_34), .W(8'hfe), .P(weight_multiplier_34_p));
  Weight_Multiplier weight_multiplier_35 (.S(I_35), .W(8'hfd), .P(weight_multiplier_35_p));
  Weight_Multiplier weight_multiplier_36 (.S(I_36), .W({8{1'b1}}), .P(weight_multiplier_36_p));
  Weight_Multiplier weight_multiplier_37 (.S(I_37), .W({8{1'b0}}), .P(weight_multiplier_37_p));
  Weight_Multiplier weight_multiplier_38 (.S(I_38), .W(8'hfd), .P(weight_multiplier_38_p));
  Weight_Multiplier weight_multiplier_39 (.S(I_39), .W(8'hfd), .P(weight_multiplier_39_p));
  Weight_Multiplier weight_multiplier_40 (.S(I_40), .W({8{1'b0}}), .P(weight_multiplier_40_p));
  Weight_Multiplier weight_multiplier_41 (.S(I_41), .W({8{1'b0}}), .P(weight_multiplier_41_p));
  Weight_Multiplier weight_multiplier_42 (.S(I_42), .W(8'h2), .P(weight_multiplier_42_p));
  Weight_Multiplier weight_multiplier_43 (.S(I_43), .W({8{1'b0}}), .P(weight_multiplier_43_p));
  Weight_Multiplier weight_multiplier_44 (.S(I_44), .W(8'h3), .P(weight_multiplier_44_p));
  Weight_Multiplier weight_multiplier_45 (.S(I_45), .W(8'hfe), .P(weight_multiplier_45_p));
  Weight_Multiplier weight_multiplier_46 (.S(I_46), .W(8'hfd), .P(weight_multiplier_46_p));
  Weight_Multiplier weight_multiplier_47 (.S(I_47), .W({8{1'b1}}), .P(weight_multiplier_47_p));
  Weight_Multiplier weight_multiplier_48 (.S(I_48), .W({8{1'b0}}), .P(weight_multiplier_48_p));
  Weight_Multiplier weight_multiplier_49 (.S(I_49), .W({8{1'b1}}), .P(weight_multiplier_49_p));
  Weight_Multiplier weight_multiplier_50 (.S(I_50), .W(8'h3), .P(weight_multiplier_50_p));
  Weight_Multiplier weight_multiplier_51 (.S(I_51), .W(8'h1), .P(weight_multiplier_51_p));
  Weight_Multiplier weight_multiplier_52 (.S(I_52), .W(8'h2), .P(weight_multiplier_52_p));
  Weight_Multiplier weight_multiplier_53 (.S(I_53), .W(8'h2), .P(weight_multiplier_53_p));
  Weight_Multiplier weight_multiplier_54 (.S(I_54), .W(8'h3), .P(weight_multiplier_54_p));
  Weight_Multiplier weight_multiplier_55 (.S(I_55), .W(8'h1), .P(weight_multiplier_55_p));
  Weight_Multiplier weight_multiplier_56 (.S(I_56), .W(8'hfe), .P(weight_multiplier_56_p));
  Weight_Multiplier weight_multiplier_57 (.S(I_57), .W({8{1'b0}}), .P(weight_multiplier_57_p));
  Weight_Multiplier weight_multiplier_58 (.S(I_58), .W(8'h2), .P(weight_multiplier_58_p));
  Weight_Multiplier weight_multiplier_59 (.S(I_59), .W(8'h1), .P(weight_multiplier_59_p));
  Weight_Multiplier weight_multiplier_60 (.S(I_60), .W({8{1'b0}}), .P(weight_multiplier_60_p));
  Weight_Multiplier weight_multiplier_61 (.S(I_61), .W(8'h2), .P(weight_multiplier_61_p));
  Weight_Multiplier weight_multiplier_62 (.S(I_62), .W(8'h2), .P(weight_multiplier_62_p));
  Weight_Multiplier weight_multiplier_63 (.S(I_63), .W(8'h2), .P(weight_multiplier_63_p));
  Weight_Multiplier weight_multiplier_64 (.S(I_64), .W(8'h3), .P(weight_multiplier_64_p));
  Adder_Tree_8_Bit adder_tree_8_bit_1 (
    .A(weight_multiplier_1_p), .B(weight_multiplier_2_p), .C(weight_multiplier_3_p),
    .D(weight_multiplier_4_p), .E(weight_multiplier_5_p), .F(weight_multiplier_6_p),
    .G(weight_multiplier_7_p), .H(weight_multiplier_8_p), .S(adder_tree_8_bit_1_s));
  Adder_Tree_8_Bit adder_tree_8_bit_2 (
    .A(weight_multiplier_9_p), .B(weight_multiplier_10_p), .C(weight_multiplier_11_p),
    .D(weight_multiplier_12_p), .E(weight_multiplier_13_p), .F(weight_multiplier_14_p),
    .G(weight_multiplier_15_p), .H(weight_multiplier_16_p), .S(adder_tree_8_bit_2_s));
  Adder_Tree_8_Bit adder_tree_8_bit_3 (
    .A(weight_multiplier_17_p), .B(weight_multiplier_18_p), .C(weight_multiplier_19_p),
    .D(weight_multiplier_20_p), .E(weight_multiplier_21_p), .F(weight_multiplier_22_p),
    .G(weight_multiplier_23_p), .H(weight_multiplier_24_p), .S(adder_tree_8_bit_3_s));
  Adder_Tree_8_Bit adder_tree_8_bit_4 (
    .A(weight_multiplier_25_p), .B(weight_multiplier_26_p), .C(weight_multiplier_27_p),
    .D(weight_multiplier_28_p), .E(weight_multiplier_29_p), .F(weight_multiplier_30_p),
    .G(weight_multiplier_31_p), .H(weight_multiplier_32_p), .S(adder_tree_8_bit_4_s));
  Adder_Tree_8_Bit adder_tree_8_bit_5 (
    .A(weight_multiplier_33_p), .B(weight_multiplier_34_p), .C(weight_multiplier_35_p),
    .D(weight_multiplier_36_p), .E(weight_multiplier_37_p), .F(weight_multiplier_38_p),
    .G(weight_multiplier_39_p), .H(weight_multiplier_40_p), .S(adder_tree_8_bit_5_s));
  Adder_Tree_8_Bit adder_tree_8_bit_6 (
    .A(weight_multiplier_41_p), .B(weight_multiplier_42_p), .C(weight_multiplier_43_p),
    .D(weight_multiplier_44_p), .E(weight_multiplier_45_p), .F(weight_multiplier_46_p),
    .G(weight_multiplier_47_p), .H(weight_multiplier_48_p), .S(adder_tree_8_bit_6_s));
  Adder_Tree_8_Bit adder_tree_8_bit_7 (
    .A(weight_multiplier_49_p), .B(weight_multiplier_50_p), .C(weight_multiplier_51_p),
    .D(weight_multiplier_52_p), .E(weight_multiplier_53_p), .F(weight_multiplier_54_p),
    .G(weight_multiplier_55_p), .H(weight_multiplier_56_p), .S(adder_tree_8_bit_7_s));
  Adder_Tree_8_Bit adder_tree_8_bit_8 (
    .A(weight_multiplier_57_p), .B(weight_multiplier_58_p), .C(weight_multiplier_59_p),
    .D(weight_multiplier_60_p), .E(weight_multiplier_61_p), .F(weight_multiplier_62_p),
    .G(weight_multiplier_63_p), .H(weight_multiplier_64_p), .S(adder_tree_8_bit_8_s));
  Adder_Tree_8_Bit adder_tree_8_bit_9 (
    .A(adder_tree_8_bit_1_s), .B(adder_tree_8_bit_2_s), .C(adder_tree_8_bit_3_s), .D(adder_tree_8_bit_4_s),
    .E(adder_tree_8_bit_5_s), .F(adder_tree_8_bit_6_s), .G(adder_tree_8_bit_7_s), .H(adder_tree_8_bit_8_s),
    .S(adder_tree_8_bit_9_s));
  Adder_8_Bit_Bus adder_8_bit_bus_1 (.A(adder_tree_8_bit_9_s), .B({8{1'b0}}), .Cin(1'b0), .S(Score_2));  // open: Cout
endmodule

module Perceptron_3 (
  input  I_1,
  input  I_2,
  input  I_3,
  input  I_4,
  input  I_5,
  input  I_6,
  input  I_7,
  input  I_8,
  input  I_9,
  input  I_10,
  input  I_11,
  input  I_12,
  input  I_13,
  input  I_14,
  input  I_15,
  input  I_16,
  input  I_17,
  input  I_18,
  input  I_19,
  input  I_20,
  input  I_21,
  input  I_22,
  input  I_23,
  input  I_24,
  input  I_25,
  input  I_26,
  input  I_27,
  input  I_28,
  input  I_29,
  input  I_30,
  input  I_31,
  input  I_32,
  input  I_33,
  input  I_34,
  input  I_35,
  input  I_36,
  input  I_37,
  input  I_38,
  input  I_39,
  input  I_40,
  input  I_41,
  input  I_42,
  input  I_43,
  input  I_44,
  input  I_45,
  input  I_46,
  input  I_47,
  input  I_48,
  input  I_49,
  input  I_50,
  input  I_51,
  input  I_52,
  input  I_53,
  input  I_54,
  input  I_55,
  input  I_56,
  input  I_57,
  input  I_58,
  input  I_59,
  input  I_60,
  input  I_61,
  input  I_62,
  input  I_63,
  input  I_64,
  output [7:0] Score_3
);

  wire [7:0] adder_tree_8_bit_1_s, adder_tree_8_bit_2_s, adder_tree_8_bit_3_s, adder_tree_8_bit_4_s,
       adder_tree_8_bit_5_s, adder_tree_8_bit_6_s, adder_tree_8_bit_7_s, adder_tree_8_bit_8_s,
       adder_tree_8_bit_9_s, weight_multiplier_1_p, weight_multiplier_2_p, weight_multiplier_3_p,
       weight_multiplier_4_p, weight_multiplier_5_p, weight_multiplier_6_p, weight_multiplier_7_p,
       weight_multiplier_8_p, weight_multiplier_9_p, weight_multiplier_10_p, weight_multiplier_11_p,
       weight_multiplier_12_p, weight_multiplier_13_p, weight_multiplier_14_p, weight_multiplier_15_p,
       weight_multiplier_16_p, weight_multiplier_17_p, weight_multiplier_18_p, weight_multiplier_19_p,
       weight_multiplier_20_p, weight_multiplier_21_p, weight_multiplier_22_p, weight_multiplier_23_p,
       weight_multiplier_24_p, weight_multiplier_25_p, weight_multiplier_26_p, weight_multiplier_27_p,
       weight_multiplier_28_p, weight_multiplier_29_p, weight_multiplier_30_p, weight_multiplier_31_p,
       weight_multiplier_32_p, weight_multiplier_33_p, weight_multiplier_34_p, weight_multiplier_35_p,
       weight_multiplier_36_p, weight_multiplier_37_p, weight_multiplier_38_p, weight_multiplier_39_p,
       weight_multiplier_40_p, weight_multiplier_41_p, weight_multiplier_42_p, weight_multiplier_43_p,
       weight_multiplier_44_p, weight_multiplier_45_p, weight_multiplier_46_p, weight_multiplier_47_p,
       weight_multiplier_48_p, weight_multiplier_49_p, weight_multiplier_50_p, weight_multiplier_51_p,
       weight_multiplier_52_p, weight_multiplier_53_p, weight_multiplier_54_p, weight_multiplier_55_p,
       weight_multiplier_56_p, weight_multiplier_57_p, weight_multiplier_58_p, weight_multiplier_59_p,
       weight_multiplier_60_p, weight_multiplier_61_p, weight_multiplier_62_p, weight_multiplier_63_p,
       weight_multiplier_64_p;

  Weight_Multiplier weight_multiplier_1 (.S(I_1), .W({8{1'b0}}), .P(weight_multiplier_1_p));
  Weight_Multiplier weight_multiplier_2 (.S(I_2), .W({8{1'b1}}), .P(weight_multiplier_2_p));
  Weight_Multiplier weight_multiplier_3 (.S(I_3), .W({8{1'b0}}), .P(weight_multiplier_3_p));
  Weight_Multiplier weight_multiplier_4 (.S(I_4), .W({8{1'b0}}), .P(weight_multiplier_4_p));
  Weight_Multiplier weight_multiplier_5 (.S(I_5), .W(8'h4), .P(weight_multiplier_5_p));
  Weight_Multiplier weight_multiplier_6 (.S(I_6), .W(8'h1), .P(weight_multiplier_6_p));
  Weight_Multiplier weight_multiplier_7 (.S(I_7), .W(8'hfe), .P(weight_multiplier_7_p));
  Weight_Multiplier weight_multiplier_8 (.S(I_8), .W({8{1'b1}}), .P(weight_multiplier_8_p));
  Weight_Multiplier weight_multiplier_9 (.S(I_9), .W({8{1'b0}}), .P(weight_multiplier_9_p));
  Weight_Multiplier weight_multiplier_10 (.S(I_10), .W(8'h2), .P(weight_multiplier_10_p));
  Weight_Multiplier weight_multiplier_11 (.S(I_11), .W(8'h2), .P(weight_multiplier_11_p));
  Weight_Multiplier weight_multiplier_12 (.S(I_12), .W({8{1'b0}}), .P(weight_multiplier_12_p));
  Weight_Multiplier weight_multiplier_13 (.S(I_13), .W({8{1'b0}}), .P(weight_multiplier_13_p));
  Weight_Multiplier weight_multiplier_14 (.S(I_14), .W(8'h1), .P(weight_multiplier_14_p));
  Weight_Multiplier weight_multiplier_15 (.S(I_15), .W(8'h3), .P(weight_multiplier_15_p));
  Weight_Multiplier weight_multiplier_16 (.S(I_16), .W(8'hfe), .P(weight_multiplier_16_p));
  Weight_Multiplier weight_multiplier_17 (.S(I_17), .W({8{1'b0}}), .P(weight_multiplier_17_p));
  Weight_Multiplier weight_multiplier_18 (.S(I_18), .W({8{1'b0}}), .P(weight_multiplier_18_p));
  Weight_Multiplier weight_multiplier_19 (.S(I_19), .W(8'hfd), .P(weight_multiplier_19_p));
  Weight_Multiplier weight_multiplier_20 (.S(I_20), .W(8'hfd), .P(weight_multiplier_20_p));
  Weight_Multiplier weight_multiplier_21 (.S(I_21), .W(8'h2), .P(weight_multiplier_21_p));
  Weight_Multiplier weight_multiplier_22 (.S(I_22), .W({8{1'b1}}), .P(weight_multiplier_22_p));
  Weight_Multiplier weight_multiplier_23 (.S(I_23), .W({8{1'b1}}), .P(weight_multiplier_23_p));
  Weight_Multiplier weight_multiplier_24 (.S(I_24), .W({8{1'b1}}), .P(weight_multiplier_24_p));
  Weight_Multiplier weight_multiplier_25 (.S(I_25), .W({8{1'b0}}), .P(weight_multiplier_25_p));
  Weight_Multiplier weight_multiplier_26 (.S(I_26), .W(8'hfe), .P(weight_multiplier_26_p));
  Weight_Multiplier weight_multiplier_27 (.S(I_27), .W(8'hfd), .P(weight_multiplier_27_p));
  Weight_Multiplier weight_multiplier_28 (.S(I_28), .W({8{1'b0}}), .P(weight_multiplier_28_p));
  Weight_Multiplier weight_multiplier_29 (.S(I_29), .W(8'h1), .P(weight_multiplier_29_p));
  Weight_Multiplier weight_multiplier_30 (.S(I_30), .W(8'hfd), .P(weight_multiplier_30_p));
  Weight_Multiplier weight_multiplier_31 (.S(I_31), .W(8'hfd), .P(weight_multiplier_31_p));
  Weight_Multiplier weight_multiplier_32 (.S(I_32), .W({8{1'b0}}), .P(weight_multiplier_32_p));
  Weight_Multiplier weight_multiplier_33 (.S(I_33), .W({8{1'b0}}), .P(weight_multiplier_33_p));
  Weight_Multiplier weight_multiplier_34 (.S(I_34), .W(8'hfe), .P(weight_multiplier_34_p));
  Weight_Multiplier weight_multiplier_35 (.S(I_35), .W({8{1'b1}}), .P(weight_multiplier_35_p));
  Weight_Multiplier weight_multiplier_36 (.S(I_36), .W({8{1'b1}}), .P(weight_multiplier_36_p));
  Weight_Multiplier weight_multiplier_37 (.S(I_37), .W(8'h3), .P(weight_multiplier_37_p));
  Weight_Multiplier weight_multiplier_38 (.S(I_38), .W({8{1'b0}}), .P(weight_multiplier_38_p));
  Weight_Multiplier weight_multiplier_39 (.S(I_39), .W(8'hfe), .P(weight_multiplier_39_p));
  Weight_Multiplier weight_multiplier_40 (.S(I_40), .W({8{1'b0}}), .P(weight_multiplier_40_p));
  Weight_Multiplier weight_multiplier_41 (.S(I_41), .W({8{1'b0}}), .P(weight_multiplier_41_p));
  Weight_Multiplier weight_multiplier_42 (.S(I_42), .W({8{1'b1}}), .P(weight_multiplier_42_p));
  Weight_Multiplier weight_multiplier_43 (.S(I_43), .W(8'hfe), .P(weight_multiplier_43_p));
  Weight_Multiplier weight_multiplier_44 (.S(I_44), .W(8'hfd), .P(weight_multiplier_44_p));
  Weight_Multiplier weight_multiplier_45 (.S(I_45), .W({8{1'b1}}), .P(weight_multiplier_45_p));
  Weight_Multiplier weight_multiplier_46 (.S(I_46), .W(8'h3), .P(weight_multiplier_46_p));
  Weight_Multiplier weight_multiplier_47 (.S(I_47), .W(8'h3), .P(weight_multiplier_47_p));
  Weight_Multiplier weight_multiplier_48 (.S(I_48), .W({8{1'b0}}), .P(weight_multiplier_48_p));
  Weight_Multiplier weight_multiplier_49 (.S(I_49), .W({8{1'b1}}), .P(weight_multiplier_49_p));
  Weight_Multiplier weight_multiplier_50 (.S(I_50), .W(8'h2), .P(weight_multiplier_50_p));
  Weight_Multiplier weight_multiplier_51 (.S(I_51), .W({8{1'b1}}), .P(weight_multiplier_51_p));
  Weight_Multiplier weight_multiplier_52 (.S(I_52), .W({8{1'b1}}), .P(weight_multiplier_52_p));
  Weight_Multiplier weight_multiplier_53 (.S(I_53), .W({8{1'b0}}), .P(weight_multiplier_53_p));
  Weight_Multiplier weight_multiplier_54 (.S(I_54), .W(8'h1), .P(weight_multiplier_54_p));
  Weight_Multiplier weight_multiplier_55 (.S(I_55), .W(8'h2), .P(weight_multiplier_55_p));
  Weight_Multiplier weight_multiplier_56 (.S(I_56), .W({8{1'b1}}), .P(weight_multiplier_56_p));
  Weight_Multiplier weight_multiplier_57 (.S(I_57), .W({8{1'b0}}), .P(weight_multiplier_57_p));
  Weight_Multiplier weight_multiplier_58 (.S(I_58), .W({8{1'b1}}), .P(weight_multiplier_58_p));
  Weight_Multiplier weight_multiplier_59 (.S(I_59), .W(8'h1), .P(weight_multiplier_59_p));
  Weight_Multiplier weight_multiplier_60 (.S(I_60), .W(8'h3), .P(weight_multiplier_60_p));
  Weight_Multiplier weight_multiplier_61 (.S(I_61), .W(8'h1), .P(weight_multiplier_61_p));
  Weight_Multiplier weight_multiplier_62 (.S(I_62), .W({8{1'b0}}), .P(weight_multiplier_62_p));
  Weight_Multiplier weight_multiplier_63 (.S(I_63), .W(8'hfe), .P(weight_multiplier_63_p));
  Weight_Multiplier weight_multiplier_64 (.S(I_64), .W(8'hfc), .P(weight_multiplier_64_p));
  Adder_Tree_8_Bit adder_tree_8_bit_1 (
    .A(weight_multiplier_1_p), .B(weight_multiplier_2_p), .C(weight_multiplier_3_p),
    .D(weight_multiplier_4_p), .E(weight_multiplier_5_p), .F(weight_multiplier_6_p),
    .G(weight_multiplier_7_p), .H(weight_multiplier_8_p), .S(adder_tree_8_bit_1_s));
  Adder_Tree_8_Bit adder_tree_8_bit_2 (
    .A(weight_multiplier_9_p), .B(weight_multiplier_10_p), .C(weight_multiplier_11_p),
    .D(weight_multiplier_12_p), .E(weight_multiplier_13_p), .F(weight_multiplier_14_p),
    .G(weight_multiplier_15_p), .H(weight_multiplier_16_p), .S(adder_tree_8_bit_2_s));
  Adder_Tree_8_Bit adder_tree_8_bit_3 (
    .A(weight_multiplier_17_p), .B(weight_multiplier_18_p), .C(weight_multiplier_19_p),
    .D(weight_multiplier_20_p), .E(weight_multiplier_21_p), .F(weight_multiplier_22_p),
    .G(weight_multiplier_23_p), .H(weight_multiplier_24_p), .S(adder_tree_8_bit_3_s));
  Adder_Tree_8_Bit adder_tree_8_bit_4 (
    .A(weight_multiplier_25_p), .B(weight_multiplier_26_p), .C(weight_multiplier_27_p),
    .D(weight_multiplier_28_p), .E(weight_multiplier_29_p), .F(weight_multiplier_30_p),
    .G(weight_multiplier_31_p), .H(weight_multiplier_32_p), .S(adder_tree_8_bit_4_s));
  Adder_Tree_8_Bit adder_tree_8_bit_5 (
    .A(weight_multiplier_33_p), .B(weight_multiplier_34_p), .C(weight_multiplier_35_p),
    .D(weight_multiplier_36_p), .E(weight_multiplier_37_p), .F(weight_multiplier_38_p),
    .G(weight_multiplier_39_p), .H(weight_multiplier_40_p), .S(adder_tree_8_bit_5_s));
  Adder_Tree_8_Bit adder_tree_8_bit_6 (
    .A(weight_multiplier_41_p), .B(weight_multiplier_42_p), .C(weight_multiplier_43_p),
    .D(weight_multiplier_44_p), .E(weight_multiplier_45_p), .F(weight_multiplier_46_p),
    .G(weight_multiplier_47_p), .H(weight_multiplier_48_p), .S(adder_tree_8_bit_6_s));
  Adder_Tree_8_Bit adder_tree_8_bit_7 (
    .A(weight_multiplier_49_p), .B(weight_multiplier_50_p), .C(weight_multiplier_51_p),
    .D(weight_multiplier_52_p), .E(weight_multiplier_53_p), .F(weight_multiplier_54_p),
    .G(weight_multiplier_55_p), .H(weight_multiplier_56_p), .S(adder_tree_8_bit_7_s));
  Adder_Tree_8_Bit adder_tree_8_bit_8 (
    .A(weight_multiplier_57_p), .B(weight_multiplier_58_p), .C(weight_multiplier_59_p),
    .D(weight_multiplier_60_p), .E(weight_multiplier_61_p), .F(weight_multiplier_62_p),
    .G(weight_multiplier_63_p), .H(weight_multiplier_64_p), .S(adder_tree_8_bit_8_s));
  Adder_Tree_8_Bit adder_tree_8_bit_9 (
    .A(adder_tree_8_bit_1_s), .B(adder_tree_8_bit_2_s), .C(adder_tree_8_bit_3_s), .D(adder_tree_8_bit_4_s),
    .E(adder_tree_8_bit_5_s), .F(adder_tree_8_bit_6_s), .G(adder_tree_8_bit_7_s), .H(adder_tree_8_bit_8_s),
    .S(adder_tree_8_bit_9_s));
  Adder_8_Bit_Bus adder_8_bit_bus_1 (.A(adder_tree_8_bit_9_s), .B(8'h1), .Cin(1'b0), .S(Score_3));  // open: Cout
endmodule

module Perceptron_4 (
  input  I_1,
  input  I_2,
  input  I_3,
  input  I_4,
  input  I_5,
  input  I_6,
  input  I_7,
  input  I_8,
  input  I_9,
  input  I_10,
  input  I_11,
  input  I_12,
  input  I_13,
  input  I_14,
  input  I_15,
  input  I_16,
  input  I_17,
  input  I_18,
  input  I_19,
  input  I_20,
  input  I_21,
  input  I_22,
  input  I_23,
  input  I_24,
  input  I_25,
  input  I_26,
  input  I_27,
  input  I_28,
  input  I_29,
  input  I_30,
  input  I_31,
  input  I_32,
  input  I_33,
  input  I_34,
  input  I_35,
  input  I_36,
  input  I_37,
  input  I_38,
  input  I_39,
  input  I_40,
  input  I_41,
  input  I_42,
  input  I_43,
  input  I_44,
  input  I_45,
  input  I_46,
  input  I_47,
  input  I_48,
  input  I_49,
  input  I_50,
  input  I_51,
  input  I_52,
  input  I_53,
  input  I_54,
  input  I_55,
  input  I_56,
  input  I_57,
  input  I_58,
  input  I_59,
  input  I_60,
  input  I_61,
  input  I_62,
  input  I_63,
  input  I_64,
  output [7:0] Score_4
);

  wire [7:0] adder_tree_8_bit_1_s, adder_tree_8_bit_2_s, adder_tree_8_bit_3_s, adder_tree_8_bit_4_s,
       adder_tree_8_bit_5_s, adder_tree_8_bit_6_s, adder_tree_8_bit_7_s, adder_tree_8_bit_8_s,
       adder_tree_8_bit_9_s, weight_multiplier_1_p, weight_multiplier_2_p, weight_multiplier_3_p,
       weight_multiplier_4_p, weight_multiplier_5_p, weight_multiplier_6_p, weight_multiplier_7_p,
       weight_multiplier_8_p, weight_multiplier_9_p, weight_multiplier_10_p, weight_multiplier_11_p,
       weight_multiplier_12_p, weight_multiplier_13_p, weight_multiplier_14_p, weight_multiplier_15_p,
       weight_multiplier_16_p, weight_multiplier_17_p, weight_multiplier_18_p, weight_multiplier_19_p,
       weight_multiplier_20_p, weight_multiplier_21_p, weight_multiplier_22_p, weight_multiplier_23_p,
       weight_multiplier_24_p, weight_multiplier_25_p, weight_multiplier_26_p, weight_multiplier_27_p,
       weight_multiplier_28_p, weight_multiplier_29_p, weight_multiplier_30_p, weight_multiplier_31_p,
       weight_multiplier_32_p, weight_multiplier_33_p, weight_multiplier_34_p, weight_multiplier_35_p,
       weight_multiplier_36_p, weight_multiplier_37_p, weight_multiplier_38_p, weight_multiplier_39_p,
       weight_multiplier_40_p, weight_multiplier_41_p, weight_multiplier_42_p, weight_multiplier_43_p,
       weight_multiplier_44_p, weight_multiplier_45_p, weight_multiplier_46_p, weight_multiplier_47_p,
       weight_multiplier_48_p, weight_multiplier_49_p, weight_multiplier_50_p, weight_multiplier_51_p,
       weight_multiplier_52_p, weight_multiplier_53_p, weight_multiplier_54_p, weight_multiplier_55_p,
       weight_multiplier_56_p, weight_multiplier_57_p, weight_multiplier_58_p, weight_multiplier_59_p,
       weight_multiplier_60_p, weight_multiplier_61_p, weight_multiplier_62_p, weight_multiplier_63_p,
       weight_multiplier_64_p;

  Weight_Multiplier weight_multiplier_1 (.S(I_1), .W({8{1'b0}}), .P(weight_multiplier_1_p));
  Weight_Multiplier weight_multiplier_2 (.S(I_2), .W({8{1'b1}}), .P(weight_multiplier_2_p));
  Weight_Multiplier weight_multiplier_3 (.S(I_3), .W(8'hfe), .P(weight_multiplier_3_p));
  Weight_Multiplier weight_multiplier_4 (.S(I_4), .W(8'hfe), .P(weight_multiplier_4_p));
  Weight_Multiplier weight_multiplier_5 (.S(I_5), .W({8{1'b1}}), .P(weight_multiplier_5_p));
  Weight_Multiplier weight_multiplier_6 (.S(I_6), .W(8'hfd), .P(weight_multiplier_6_p));
  Weight_Multiplier weight_multiplier_7 (.S(I_7), .W(8'hfd), .P(weight_multiplier_7_p));
  Weight_Multiplier weight_multiplier_8 (.S(I_8), .W(8'h4), .P(weight_multiplier_8_p));
  Weight_Multiplier weight_multiplier_9 (.S(I_9), .W({8{1'b0}}), .P(weight_multiplier_9_p));
  Weight_Multiplier weight_multiplier_10 (.S(I_10), .W({8{1'b1}}), .P(weight_multiplier_10_p));
  Weight_Multiplier weight_multiplier_11 (.S(I_11), .W(8'hfe), .P(weight_multiplier_11_p));
  Weight_Multiplier weight_multiplier_12 (.S(I_12), .W({8{1'b0}}), .P(weight_multiplier_12_p));
  Weight_Multiplier weight_multiplier_13 (.S(I_13), .W(8'hfc), .P(weight_multiplier_13_p));
  Weight_Multiplier weight_multiplier_14 (.S(I_14), .W(8'hfe), .P(weight_multiplier_14_p));
  Weight_Multiplier weight_multiplier_15 (.S(I_15), .W(8'hfe), .P(weight_multiplier_15_p));
  Weight_Multiplier weight_multiplier_16 (.S(I_16), .W({8{1'b0}}), .P(weight_multiplier_16_p));
  Weight_Multiplier weight_multiplier_17 (.S(I_17), .W({8{1'b0}}), .P(weight_multiplier_17_p));
  Weight_Multiplier weight_multiplier_18 (.S(I_18), .W({8{1'b0}}), .P(weight_multiplier_18_p));
  Weight_Multiplier weight_multiplier_19 (.S(I_19), .W(8'h1), .P(weight_multiplier_19_p));
  Weight_Multiplier weight_multiplier_20 (.S(I_20), .W(8'h1), .P(weight_multiplier_20_p));
  Weight_Multiplier weight_multiplier_21 (.S(I_21), .W(8'h1), .P(weight_multiplier_21_p));
  Weight_Multiplier weight_multiplier_22 (.S(I_22), .W(8'h1), .P(weight_multiplier_22_p));
  Weight_Multiplier weight_multiplier_23 (.S(I_23), .W(8'h2), .P(weight_multiplier_23_p));
  Weight_Multiplier weight_multiplier_24 (.S(I_24), .W(8'h1), .P(weight_multiplier_24_p));
  Weight_Multiplier weight_multiplier_25 (.S(I_25), .W({8{1'b0}}), .P(weight_multiplier_25_p));
  Weight_Multiplier weight_multiplier_26 (.S(I_26), .W(8'h3), .P(weight_multiplier_26_p));
  Weight_Multiplier weight_multiplier_27 (.S(I_27), .W(8'h3), .P(weight_multiplier_27_p));
  Weight_Multiplier weight_multiplier_28 (.S(I_28), .W({8{1'b1}}), .P(weight_multiplier_28_p));
  Weight_Multiplier weight_multiplier_29 (.S(I_29), .W({8{1'b0}}), .P(weight_multiplier_29_p));
  Weight_Multiplier weight_multiplier_30 (.S(I_30), .W(8'h1), .P(weight_multiplier_30_p));
  Weight_Multiplier weight_multiplier_31 (.S(I_31), .W(8'h3), .P(weight_multiplier_31_p));
  Weight_Multiplier weight_multiplier_32 (.S(I_32), .W({8{1'b0}}), .P(weight_multiplier_32_p));
  Weight_Multiplier weight_multiplier_33 (.S(I_33), .W({8{1'b0}}), .P(weight_multiplier_33_p));
  Weight_Multiplier weight_multiplier_34 (.S(I_34), .W(8'h2), .P(weight_multiplier_34_p));
  Weight_Multiplier weight_multiplier_35 (.S(I_35), .W(8'h2), .P(weight_multiplier_35_p));
  Weight_Multiplier weight_multiplier_36 (.S(I_36), .W(8'h2), .P(weight_multiplier_36_p));
  Weight_Multiplier weight_multiplier_37 (.S(I_37), .W(8'h3), .P(weight_multiplier_37_p));
  Weight_Multiplier weight_multiplier_38 (.S(I_38), .W(8'h2), .P(weight_multiplier_38_p));
  Weight_Multiplier weight_multiplier_39 (.S(I_39), .W(8'h2), .P(weight_multiplier_39_p));
  Weight_Multiplier weight_multiplier_40 (.S(I_40), .W({8{1'b0}}), .P(weight_multiplier_40_p));
  Weight_Multiplier weight_multiplier_41 (.S(I_41), .W({8{1'b0}}), .P(weight_multiplier_41_p));
  Weight_Multiplier weight_multiplier_42 (.S(I_42), .W(8'h3), .P(weight_multiplier_42_p));
  Weight_Multiplier weight_multiplier_43 (.S(I_43), .W({8{1'b0}}), .P(weight_multiplier_43_p));
  Weight_Multiplier weight_multiplier_44 (.S(I_44), .W(8'h3), .P(weight_multiplier_44_p));
  Weight_Multiplier weight_multiplier_45 (.S(I_45), .W(8'h3), .P(weight_multiplier_45_p));
  Weight_Multiplier weight_multiplier_46 (.S(I_46), .W(8'h2), .P(weight_multiplier_46_p));
  Weight_Multiplier weight_multiplier_47 (.S(I_47), .W({8{1'b1}}), .P(weight_multiplier_47_p));
  Weight_Multiplier weight_multiplier_48 (.S(I_48), .W({8{1'b0}}), .P(weight_multiplier_48_p));
  Weight_Multiplier weight_multiplier_49 (.S(I_49), .W(8'h1), .P(weight_multiplier_49_p));
  Weight_Multiplier weight_multiplier_50 (.S(I_50), .W(8'h3), .P(weight_multiplier_50_p));
  Weight_Multiplier weight_multiplier_51 (.S(I_51), .W(8'hfe), .P(weight_multiplier_51_p));
  Weight_Multiplier weight_multiplier_52 (.S(I_52), .W({8{1'b0}}), .P(weight_multiplier_52_p));
  Weight_Multiplier weight_multiplier_53 (.S(I_53), .W({8{1'b0}}), .P(weight_multiplier_53_p));
  Weight_Multiplier weight_multiplier_54 (.S(I_54), .W(8'hfe), .P(weight_multiplier_54_p));
  Weight_Multiplier weight_multiplier_55 (.S(I_55), .W(8'hfe), .P(weight_multiplier_55_p));
  Weight_Multiplier weight_multiplier_56 (.S(I_56), .W(8'hfe), .P(weight_multiplier_56_p));
  Weight_Multiplier weight_multiplier_57 (.S(I_57), .W({8{1'b0}}), .P(weight_multiplier_57_p));
  Weight_Multiplier weight_multiplier_58 (.S(I_58), .W({8{1'b1}}), .P(weight_multiplier_58_p));
  Weight_Multiplier weight_multiplier_59 (.S(I_59), .W(8'hfe), .P(weight_multiplier_59_p));
  Weight_Multiplier weight_multiplier_60 (.S(I_60), .W(8'hfe), .P(weight_multiplier_60_p));
  Weight_Multiplier weight_multiplier_61 (.S(I_61), .W({8{1'b1}}), .P(weight_multiplier_61_p));
  Weight_Multiplier weight_multiplier_62 (.S(I_62), .W(8'hfe), .P(weight_multiplier_62_p));
  Weight_Multiplier weight_multiplier_63 (.S(I_63), .W(8'hfe), .P(weight_multiplier_63_p));
  Weight_Multiplier weight_multiplier_64 (.S(I_64), .W({8{1'b1}}), .P(weight_multiplier_64_p));
  Adder_Tree_8_Bit adder_tree_8_bit_1 (
    .A(weight_multiplier_1_p), .B(weight_multiplier_2_p), .C(weight_multiplier_3_p),
    .D(weight_multiplier_4_p), .E(weight_multiplier_5_p), .F(weight_multiplier_6_p),
    .G(weight_multiplier_7_p), .H(weight_multiplier_8_p), .S(adder_tree_8_bit_1_s));
  Adder_Tree_8_Bit adder_tree_8_bit_2 (
    .A(weight_multiplier_9_p), .B(weight_multiplier_10_p), .C(weight_multiplier_11_p),
    .D(weight_multiplier_12_p), .E(weight_multiplier_13_p), .F(weight_multiplier_14_p),
    .G(weight_multiplier_15_p), .H(weight_multiplier_16_p), .S(adder_tree_8_bit_2_s));
  Adder_Tree_8_Bit adder_tree_8_bit_3 (
    .A(weight_multiplier_17_p), .B(weight_multiplier_18_p), .C(weight_multiplier_19_p),
    .D(weight_multiplier_20_p), .E(weight_multiplier_21_p), .F(weight_multiplier_22_p),
    .G(weight_multiplier_23_p), .H(weight_multiplier_24_p), .S(adder_tree_8_bit_3_s));
  Adder_Tree_8_Bit adder_tree_8_bit_4 (
    .A(weight_multiplier_25_p), .B(weight_multiplier_26_p), .C(weight_multiplier_27_p),
    .D(weight_multiplier_28_p), .E(weight_multiplier_29_p), .F(weight_multiplier_30_p),
    .G(weight_multiplier_31_p), .H(weight_multiplier_32_p), .S(adder_tree_8_bit_4_s));
  Adder_Tree_8_Bit adder_tree_8_bit_5 (
    .A(weight_multiplier_33_p), .B(weight_multiplier_34_p), .C(weight_multiplier_35_p),
    .D(weight_multiplier_36_p), .E(weight_multiplier_37_p), .F(weight_multiplier_38_p),
    .G(weight_multiplier_39_p), .H(weight_multiplier_40_p), .S(adder_tree_8_bit_5_s));
  Adder_Tree_8_Bit adder_tree_8_bit_6 (
    .A(weight_multiplier_41_p), .B(weight_multiplier_42_p), .C(weight_multiplier_43_p),
    .D(weight_multiplier_44_p), .E(weight_multiplier_45_p), .F(weight_multiplier_46_p),
    .G(weight_multiplier_47_p), .H(weight_multiplier_48_p), .S(adder_tree_8_bit_6_s));
  Adder_Tree_8_Bit adder_tree_8_bit_7 (
    .A(weight_multiplier_49_p), .B(weight_multiplier_50_p), .C(weight_multiplier_51_p),
    .D(weight_multiplier_52_p), .E(weight_multiplier_53_p), .F(weight_multiplier_54_p),
    .G(weight_multiplier_55_p), .H(weight_multiplier_56_p), .S(adder_tree_8_bit_7_s));
  Adder_Tree_8_Bit adder_tree_8_bit_8 (
    .A(weight_multiplier_57_p), .B(weight_multiplier_58_p), .C(weight_multiplier_59_p),
    .D(weight_multiplier_60_p), .E(weight_multiplier_61_p), .F(weight_multiplier_62_p),
    .G(weight_multiplier_63_p), .H(weight_multiplier_64_p), .S(adder_tree_8_bit_8_s));
  Adder_Tree_8_Bit adder_tree_8_bit_9 (
    .A(adder_tree_8_bit_1_s), .B(adder_tree_8_bit_2_s), .C(adder_tree_8_bit_3_s), .D(adder_tree_8_bit_4_s),
    .E(adder_tree_8_bit_5_s), .F(adder_tree_8_bit_6_s), .G(adder_tree_8_bit_7_s), .H(adder_tree_8_bit_8_s),
    .S(adder_tree_8_bit_9_s));
  Adder_8_Bit_Bus adder_8_bit_bus_1 (.A(adder_tree_8_bit_9_s), .B(8'h2), .Cin(1'b0), .S(Score_4));  // open: Cout
endmodule

module Perceptron_5 (
  input  I_1,
  input  I_2,
  input  I_3,
  input  I_4,
  input  I_5,
  input  I_6,
  input  I_7,
  input  I_8,
  input  I_9,
  input  I_10,
  input  I_11,
  input  I_12,
  input  I_13,
  input  I_14,
  input  I_15,
  input  I_16,
  input  I_17,
  input  I_18,
  input  I_19,
  input  I_20,
  input  I_21,
  input  I_22,
  input  I_23,
  input  I_24,
  input  I_25,
  input  I_26,
  input  I_27,
  input  I_28,
  input  I_29,
  input  I_30,
  input  I_31,
  input  I_32,
  input  I_33,
  input  I_34,
  input  I_35,
  input  I_36,
  input  I_37,
  input  I_38,
  input  I_39,
  input  I_40,
  input  I_41,
  input  I_42,
  input  I_43,
  input  I_44,
  input  I_45,
  input  I_46,
  input  I_47,
  input  I_48,
  input  I_49,
  input  I_50,
  input  I_51,
  input  I_52,
  input  I_53,
  input  I_54,
  input  I_55,
  input  I_56,
  input  I_57,
  input  I_58,
  input  I_59,
  input  I_60,
  input  I_61,
  input  I_62,
  input  I_63,
  input  I_64,
  output [7:0] Score_5
);

  wire [7:0] adder_tree_8_bit_1_s, adder_tree_8_bit_2_s, adder_tree_8_bit_3_s, adder_tree_8_bit_4_s,
       adder_tree_8_bit_5_s, adder_tree_8_bit_6_s, adder_tree_8_bit_7_s, adder_tree_8_bit_8_s,
       adder_tree_8_bit_9_s, weight_multiplier_1_p, weight_multiplier_2_p, weight_multiplier_3_p,
       weight_multiplier_4_p, weight_multiplier_5_p, weight_multiplier_6_p, weight_multiplier_7_p,
       weight_multiplier_8_p, weight_multiplier_9_p, weight_multiplier_10_p, weight_multiplier_11_p,
       weight_multiplier_12_p, weight_multiplier_13_p, weight_multiplier_14_p, weight_multiplier_15_p,
       weight_multiplier_16_p, weight_multiplier_17_p, weight_multiplier_18_p, weight_multiplier_19_p,
       weight_multiplier_20_p, weight_multiplier_21_p, weight_multiplier_22_p, weight_multiplier_23_p,
       weight_multiplier_24_p, weight_multiplier_25_p, weight_multiplier_26_p, weight_multiplier_27_p,
       weight_multiplier_28_p, weight_multiplier_29_p, weight_multiplier_30_p, weight_multiplier_31_p,
       weight_multiplier_32_p, weight_multiplier_33_p, weight_multiplier_34_p, weight_multiplier_35_p,
       weight_multiplier_36_p, weight_multiplier_37_p, weight_multiplier_38_p, weight_multiplier_39_p,
       weight_multiplier_40_p, weight_multiplier_41_p, weight_multiplier_42_p, weight_multiplier_43_p,
       weight_multiplier_44_p, weight_multiplier_45_p, weight_multiplier_46_p, weight_multiplier_47_p,
       weight_multiplier_48_p, weight_multiplier_49_p, weight_multiplier_50_p, weight_multiplier_51_p,
       weight_multiplier_52_p, weight_multiplier_53_p, weight_multiplier_54_p, weight_multiplier_55_p,
       weight_multiplier_56_p, weight_multiplier_57_p, weight_multiplier_58_p, weight_multiplier_59_p,
       weight_multiplier_60_p, weight_multiplier_61_p, weight_multiplier_62_p, weight_multiplier_63_p,
       weight_multiplier_64_p;

  Weight_Multiplier weight_multiplier_1 (.S(I_1), .W({8{1'b0}}), .P(weight_multiplier_1_p));
  Weight_Multiplier weight_multiplier_2 (.S(I_2), .W(8'h1), .P(weight_multiplier_2_p));
  Weight_Multiplier weight_multiplier_3 (.S(I_3), .W(8'h3), .P(weight_multiplier_3_p));
  Weight_Multiplier weight_multiplier_4 (.S(I_4), .W(8'h2), .P(weight_multiplier_4_p));
  Weight_Multiplier weight_multiplier_5 (.S(I_5), .W(8'h1), .P(weight_multiplier_5_p));
  Weight_Multiplier weight_multiplier_6 (.S(I_6), .W(8'h2), .P(weight_multiplier_6_p));
  Weight_Multiplier weight_multiplier_7 (.S(I_7), .W(8'h3), .P(weight_multiplier_7_p));
  Weight_Multiplier weight_multiplier_8 (.S(I_8), .W(8'hfc), .P(weight_multiplier_8_p));
  Weight_Multiplier weight_multiplier_9 (.S(I_9), .W({8{1'b0}}), .P(weight_multiplier_9_p));
  Weight_Multiplier weight_multiplier_10 (.S(I_10), .W({8{1'b0}}), .P(weight_multiplier_10_p));
  Weight_Multiplier weight_multiplier_11 (.S(I_11), .W(8'h2), .P(weight_multiplier_11_p));
  Weight_Multiplier weight_multiplier_12 (.S(I_12), .W(8'h3), .P(weight_multiplier_12_p));
  Weight_Multiplier weight_multiplier_13 (.S(I_13), .W({8{1'b0}}), .P(weight_multiplier_13_p));
  Weight_Multiplier weight_multiplier_14 (.S(I_14), .W({8{1'b1}}), .P(weight_multiplier_14_p));
  Weight_Multiplier weight_multiplier_15 (.S(I_15), .W(8'h1), .P(weight_multiplier_15_p));
  Weight_Multiplier weight_multiplier_16 (.S(I_16), .W(8'hfc), .P(weight_multiplier_16_p));
  Weight_Multiplier weight_multiplier_17 (.S(I_17), .W({8{1'b0}}), .P(weight_multiplier_17_p));
  Weight_Multiplier weight_multiplier_18 (.S(I_18), .W(8'h1), .P(weight_multiplier_18_p));
  Weight_Multiplier weight_multiplier_19 (.S(I_19), .W(8'h3), .P(weight_multiplier_19_p));
  Weight_Multiplier weight_multiplier_20 (.S(I_20), .W({8{1'b0}}), .P(weight_multiplier_20_p));
  Weight_Multiplier weight_multiplier_21 (.S(I_21), .W(8'hfd), .P(weight_multiplier_21_p));
  Weight_Multiplier weight_multiplier_22 (.S(I_22), .W(8'hfd), .P(weight_multiplier_22_p));
  Weight_Multiplier weight_multiplier_23 (.S(I_23), .W(8'hfc), .P(weight_multiplier_23_p));
  Weight_Multiplier weight_multiplier_24 (.S(I_24), .W(8'hfe), .P(weight_multiplier_24_p));
  Weight_Multiplier weight_multiplier_25 (.S(I_25), .W({8{1'b0}}), .P(weight_multiplier_25_p));
  Weight_Multiplier weight_multiplier_26 (.S(I_26), .W(8'h1), .P(weight_multiplier_26_p));
  Weight_Multiplier weight_multiplier_27 (.S(I_27), .W(8'h3), .P(weight_multiplier_27_p));
  Weight_Multiplier weight_multiplier_28 (.S(I_28), .W(8'h2), .P(weight_multiplier_28_p));
  Weight_Multiplier weight_multiplier_29 (.S(I_29), .W(8'h2), .P(weight_multiplier_29_p));
  Weight_Multiplier weight_multiplier_30 (.S(I_30), .W(8'hfe), .P(weight_multiplier_30_p));
  Weight_Multiplier weight_multiplier_31 (.S(I_31), .W(8'hfd), .P(weight_multiplier_31_p));
  Weight_Multiplier weight_multiplier_32 (.S(I_32), .W({8{1'b0}}), .P(weight_multiplier_32_p));
  Weight_Multiplier weight_multiplier_33 (.S(I_33), .W({8{1'b0}}), .P(weight_multiplier_33_p));
  Weight_Multiplier weight_multiplier_34 (.S(I_34), .W({8{1'b0}}), .P(weight_multiplier_34_p));
  Weight_Multiplier weight_multiplier_35 (.S(I_35), .W(8'h2), .P(weight_multiplier_35_p));
  Weight_Multiplier weight_multiplier_36 (.S(I_36), .W(8'hfd), .P(weight_multiplier_36_p));
  Weight_Multiplier weight_multiplier_37 (.S(I_37), .W({8{1'b1}}), .P(weight_multiplier_37_p));
  Weight_Multiplier weight_multiplier_38 (.S(I_38), .W(8'h1), .P(weight_multiplier_38_p));
  Weight_Multiplier weight_multiplier_39 (.S(I_39), .W(8'h2), .P(weight_multiplier_39_p));
  Weight_Multiplier weight_multiplier_40 (.S(I_40), .W({8{1'b0}}), .P(weight_multiplier_40_p));
  Weight_Multiplier weight_multiplier_41 (.S(I_41), .W({8{1'b0}}), .P(weight_multiplier_41_p));
  Weight_Multiplier weight_multiplier_42 (.S(I_42), .W(8'hfd), .P(weight_multiplier_42_p));
  Weight_Multiplier weight_multiplier_43 (.S(I_43), .W(8'hfd), .P(weight_multiplier_43_p));
  Weight_Multiplier weight_multiplier_44 (.S(I_44), .W(8'hfe), .P(weight_multiplier_44_p));
  Weight_Multiplier weight_multiplier_45 (.S(I_45), .W({8{1'b1}}), .P(weight_multiplier_45_p));
  Weight_Multiplier weight_multiplier_46 (.S(I_46), .W(8'h1), .P(weight_multiplier_46_p));
  Weight_Multiplier weight_multiplier_47 (.S(I_47), .W({8{1'b0}}), .P(weight_multiplier_47_p));
  Weight_Multiplier weight_multiplier_48 (.S(I_48), .W({8{1'b0}}), .P(weight_multiplier_48_p));
  Weight_Multiplier weight_multiplier_49 (.S(I_49), .W({8{1'b1}}), .P(weight_multiplier_49_p));
  Weight_Multiplier weight_multiplier_50 (.S(I_50), .W(8'hfd), .P(weight_multiplier_50_p));
  Weight_Multiplier weight_multiplier_51 (.S(I_51), .W({8{1'b1}}), .P(weight_multiplier_51_p));
  Weight_Multiplier weight_multiplier_52 (.S(I_52), .W(8'hfe), .P(weight_multiplier_52_p));
  Weight_Multiplier weight_multiplier_53 (.S(I_53), .W(8'h1), .P(weight_multiplier_53_p));
  Weight_Multiplier weight_multiplier_54 (.S(I_54), .W({8{1'b0}}), .P(weight_multiplier_54_p));
  Weight_Multiplier weight_multiplier_55 (.S(I_55), .W({8{1'b1}}), .P(weight_multiplier_55_p));
  Weight_Multiplier weight_multiplier_56 (.S(I_56), .W({8{1'b1}}), .P(weight_multiplier_56_p));
  Weight_Multiplier weight_multiplier_57 (.S(I_57), .W({8{1'b0}}), .P(weight_multiplier_57_p));
  Weight_Multiplier weight_multiplier_58 (.S(I_58), .W(8'h1), .P(weight_multiplier_58_p));
  Weight_Multiplier weight_multiplier_59 (.S(I_59), .W(8'h3), .P(weight_multiplier_59_p));
  Weight_Multiplier weight_multiplier_60 (.S(I_60), .W(8'h1), .P(weight_multiplier_60_p));
  Weight_Multiplier weight_multiplier_61 (.S(I_61), .W({8{1'b1}}), .P(weight_multiplier_61_p));
  Weight_Multiplier weight_multiplier_62 (.S(I_62), .W(8'hfe), .P(weight_multiplier_62_p));
  Weight_Multiplier weight_multiplier_63 (.S(I_63), .W(8'hfe), .P(weight_multiplier_63_p));
  Weight_Multiplier weight_multiplier_64 (.S(I_64), .W(8'hfe), .P(weight_multiplier_64_p));
  Adder_Tree_8_Bit adder_tree_8_bit_1 (
    .A(weight_multiplier_1_p), .B(weight_multiplier_2_p), .C(weight_multiplier_3_p),
    .D(weight_multiplier_4_p), .E(weight_multiplier_5_p), .F(weight_multiplier_6_p),
    .G(weight_multiplier_7_p), .H(weight_multiplier_8_p), .S(adder_tree_8_bit_1_s));
  Adder_Tree_8_Bit adder_tree_8_bit_2 (
    .A(weight_multiplier_9_p), .B(weight_multiplier_10_p), .C(weight_multiplier_11_p),
    .D(weight_multiplier_12_p), .E(weight_multiplier_13_p), .F(weight_multiplier_14_p),
    .G(weight_multiplier_15_p), .H(weight_multiplier_16_p), .S(adder_tree_8_bit_2_s));
  Adder_Tree_8_Bit adder_tree_8_bit_3 (
    .A(weight_multiplier_17_p), .B(weight_multiplier_18_p), .C(weight_multiplier_19_p),
    .D(weight_multiplier_20_p), .E(weight_multiplier_21_p), .F(weight_multiplier_22_p),
    .G(weight_multiplier_23_p), .H(weight_multiplier_24_p), .S(adder_tree_8_bit_3_s));
  Adder_Tree_8_Bit adder_tree_8_bit_4 (
    .A(weight_multiplier_25_p), .B(weight_multiplier_26_p), .C(weight_multiplier_27_p),
    .D(weight_multiplier_28_p), .E(weight_multiplier_29_p), .F(weight_multiplier_30_p),
    .G(weight_multiplier_31_p), .H(weight_multiplier_32_p), .S(adder_tree_8_bit_4_s));
  Adder_Tree_8_Bit adder_tree_8_bit_5 (
    .A(weight_multiplier_33_p), .B(weight_multiplier_34_p), .C(weight_multiplier_35_p),
    .D(weight_multiplier_36_p), .E(weight_multiplier_37_p), .F(weight_multiplier_38_p),
    .G(weight_multiplier_39_p), .H(weight_multiplier_40_p), .S(adder_tree_8_bit_5_s));
  Adder_Tree_8_Bit adder_tree_8_bit_6 (
    .A(weight_multiplier_41_p), .B(weight_multiplier_42_p), .C(weight_multiplier_43_p),
    .D(weight_multiplier_44_p), .E(weight_multiplier_45_p), .F(weight_multiplier_46_p),
    .G(weight_multiplier_47_p), .H(weight_multiplier_48_p), .S(adder_tree_8_bit_6_s));
  Adder_Tree_8_Bit adder_tree_8_bit_7 (
    .A(weight_multiplier_49_p), .B(weight_multiplier_50_p), .C(weight_multiplier_51_p),
    .D(weight_multiplier_52_p), .E(weight_multiplier_53_p), .F(weight_multiplier_54_p),
    .G(weight_multiplier_55_p), .H(weight_multiplier_56_p), .S(adder_tree_8_bit_7_s));
  Adder_Tree_8_Bit adder_tree_8_bit_8 (
    .A(weight_multiplier_57_p), .B(weight_multiplier_58_p), .C(weight_multiplier_59_p),
    .D(weight_multiplier_60_p), .E(weight_multiplier_61_p), .F(weight_multiplier_62_p),
    .G(weight_multiplier_63_p), .H(weight_multiplier_64_p), .S(adder_tree_8_bit_8_s));
  Adder_Tree_8_Bit adder_tree_8_bit_9 (
    .A(adder_tree_8_bit_1_s), .B(adder_tree_8_bit_2_s), .C(adder_tree_8_bit_3_s), .D(adder_tree_8_bit_4_s),
    .E(adder_tree_8_bit_5_s), .F(adder_tree_8_bit_6_s), .G(adder_tree_8_bit_7_s), .H(adder_tree_8_bit_8_s),
    .S(adder_tree_8_bit_9_s));
  Adder_8_Bit_Bus adder_8_bit_bus_1 (.A(adder_tree_8_bit_9_s), .B({8{1'b0}}), .Cin(1'b0), .S(Score_5));  // open: Cout
endmodule

module Perceptron_6 (
  input  I_1,
  input  I_2,
  input  I_3,
  input  I_4,
  input  I_5,
  input  I_6,
  input  I_7,
  input  I_8,
  input  I_9,
  input  I_10,
  input  I_11,
  input  I_12,
  input  I_13,
  input  I_14,
  input  I_15,
  input  I_16,
  input  I_17,
  input  I_18,
  input  I_19,
  input  I_20,
  input  I_21,
  input  I_22,
  input  I_23,
  input  I_24,
  input  I_25,
  input  I_26,
  input  I_27,
  input  I_28,
  input  I_29,
  input  I_30,
  input  I_31,
  input  I_32,
  input  I_33,
  input  I_34,
  input  I_35,
  input  I_36,
  input  I_37,
  input  I_38,
  input  I_39,
  input  I_40,
  input  I_41,
  input  I_42,
  input  I_43,
  input  I_44,
  input  I_45,
  input  I_46,
  input  I_47,
  input  I_48,
  input  I_49,
  input  I_50,
  input  I_51,
  input  I_52,
  input  I_53,
  input  I_54,
  input  I_55,
  input  I_56,
  input  I_57,
  input  I_58,
  input  I_59,
  input  I_60,
  input  I_61,
  input  I_62,
  input  I_63,
  input  I_64,
  output [7:0] Score_6
);

  wire [7:0] adder_tree_8_bit_1_s, adder_tree_8_bit_2_s, adder_tree_8_bit_3_s, adder_tree_8_bit_4_s,
       adder_tree_8_bit_5_s, adder_tree_8_bit_6_s, adder_tree_8_bit_7_s, adder_tree_8_bit_8_s,
       adder_tree_8_bit_9_s, weight_multiplier_1_p, weight_multiplier_2_p, weight_multiplier_3_p,
       weight_multiplier_4_p, weight_multiplier_5_p, weight_multiplier_6_p, weight_multiplier_7_p,
       weight_multiplier_8_p, weight_multiplier_9_p, weight_multiplier_10_p, weight_multiplier_11_p,
       weight_multiplier_12_p, weight_multiplier_13_p, weight_multiplier_14_p, weight_multiplier_15_p,
       weight_multiplier_16_p, weight_multiplier_17_p, weight_multiplier_18_p, weight_multiplier_19_p,
       weight_multiplier_20_p, weight_multiplier_21_p, weight_multiplier_22_p, weight_multiplier_23_p,
       weight_multiplier_24_p, weight_multiplier_25_p, weight_multiplier_26_p, weight_multiplier_27_p,
       weight_multiplier_28_p, weight_multiplier_29_p, weight_multiplier_30_p, weight_multiplier_31_p,
       weight_multiplier_32_p, weight_multiplier_33_p, weight_multiplier_34_p, weight_multiplier_35_p,
       weight_multiplier_36_p, weight_multiplier_37_p, weight_multiplier_38_p, weight_multiplier_39_p,
       weight_multiplier_40_p, weight_multiplier_41_p, weight_multiplier_42_p, weight_multiplier_43_p,
       weight_multiplier_44_p, weight_multiplier_45_p, weight_multiplier_46_p, weight_multiplier_47_p,
       weight_multiplier_48_p, weight_multiplier_49_p, weight_multiplier_50_p, weight_multiplier_51_p,
       weight_multiplier_52_p, weight_multiplier_53_p, weight_multiplier_54_p, weight_multiplier_55_p,
       weight_multiplier_56_p, weight_multiplier_57_p, weight_multiplier_58_p, weight_multiplier_59_p,
       weight_multiplier_60_p, weight_multiplier_61_p, weight_multiplier_62_p, weight_multiplier_63_p,
       weight_multiplier_64_p;

  Weight_Multiplier weight_multiplier_1 (.S(I_1), .W({8{1'b0}}), .P(weight_multiplier_1_p));
  Weight_Multiplier weight_multiplier_2 (.S(I_2), .W({8{1'b1}}), .P(weight_multiplier_2_p));
  Weight_Multiplier weight_multiplier_3 (.S(I_3), .W(8'hfe), .P(weight_multiplier_3_p));
  Weight_Multiplier weight_multiplier_4 (.S(I_4), .W({8{1'b1}}), .P(weight_multiplier_4_p));
  Weight_Multiplier weight_multiplier_5 (.S(I_5), .W({8{1'b1}}), .P(weight_multiplier_5_p));
  Weight_Multiplier weight_multiplier_6 (.S(I_6), .W({8{1'b1}}), .P(weight_multiplier_6_p));
  Weight_Multiplier weight_multiplier_7 (.S(I_7), .W({8{1'b1}}), .P(weight_multiplier_7_p));
  Weight_Multiplier weight_multiplier_8 (.S(I_8), .W({8{1'b1}}), .P(weight_multiplier_8_p));
  Weight_Multiplier weight_multiplier_9 (.S(I_9), .W({8{1'b0}}), .P(weight_multiplier_9_p));
  Weight_Multiplier weight_multiplier_10 (.S(I_10), .W(8'hfe), .P(weight_multiplier_10_p));
  Weight_Multiplier weight_multiplier_11 (.S(I_11), .W({8{1'b1}}), .P(weight_multiplier_11_p));
  Weight_Multiplier weight_multiplier_12 (.S(I_12), .W(8'h1), .P(weight_multiplier_12_p));
  Weight_Multiplier weight_multiplier_13 (.S(I_13), .W({8{1'b1}}), .P(weight_multiplier_13_p));
  Weight_Multiplier weight_multiplier_14 (.S(I_14), .W(8'hfe), .P(weight_multiplier_14_p));
  Weight_Multiplier weight_multiplier_15 (.S(I_15), .W({8{1'b1}}), .P(weight_multiplier_15_p));
  Weight_Multiplier weight_multiplier_16 (.S(I_16), .W({8{1'b1}}), .P(weight_multiplier_16_p));
  Weight_Multiplier weight_multiplier_17 (.S(I_17), .W({8{1'b0}}), .P(weight_multiplier_17_p));
  Weight_Multiplier weight_multiplier_18 (.S(I_18), .W(8'hfe), .P(weight_multiplier_18_p));
  Weight_Multiplier weight_multiplier_19 (.S(I_19), .W(8'h1), .P(weight_multiplier_19_p));
  Weight_Multiplier weight_multiplier_20 (.S(I_20), .W(8'h1), .P(weight_multiplier_20_p));
  Weight_Multiplier weight_multiplier_21 (.S(I_21), .W(8'hfe), .P(weight_multiplier_21_p));
  Weight_Multiplier weight_multiplier_22 (.S(I_22), .W(8'hfd), .P(weight_multiplier_22_p));
  Weight_Multiplier weight_multiplier_23 (.S(I_23), .W(8'hfe), .P(weight_multiplier_23_p));
  Weight_Multiplier weight_multiplier_24 (.S(I_24), .W({8{1'b1}}), .P(weight_multiplier_24_p));
  Weight_Multiplier weight_multiplier_25 (.S(I_25), .W({8{1'b0}}), .P(weight_multiplier_25_p));
  Weight_Multiplier weight_multiplier_26 (.S(I_26), .W({8{1'b1}}), .P(weight_multiplier_26_p));
  Weight_Multiplier weight_multiplier_27 (.S(I_27), .W(8'h1), .P(weight_multiplier_27_p));
  Weight_Multiplier weight_multiplier_28 (.S(I_28), .W({8{1'b0}}), .P(weight_multiplier_28_p));
  Weight_Multiplier weight_multiplier_29 (.S(I_29), .W(8'hfe), .P(weight_multiplier_29_p));
  Weight_Multiplier weight_multiplier_30 (.S(I_30), .W(8'hfe), .P(weight_multiplier_30_p));
  Weight_Multiplier weight_multiplier_31 (.S(I_31), .W(8'hfe), .P(weight_multiplier_31_p));
  Weight_Multiplier weight_multiplier_32 (.S(I_32), .W({8{1'b0}}), .P(weight_multiplier_32_p));
  Weight_Multiplier weight_multiplier_33 (.S(I_33), .W({8{1'b0}}), .P(weight_multiplier_33_p));
  Weight_Multiplier weight_multiplier_34 (.S(I_34), .W(8'h4), .P(weight_multiplier_34_p));
  Weight_Multiplier weight_multiplier_35 (.S(I_35), .W(8'h2), .P(weight_multiplier_35_p));
  Weight_Multiplier weight_multiplier_36 (.S(I_36), .W(8'h2), .P(weight_multiplier_36_p));
  Weight_Multiplier weight_multiplier_37 (.S(I_37), .W(8'h2), .P(weight_multiplier_37_p));
  Weight_Multiplier weight_multiplier_38 (.S(I_38), .W(8'h1), .P(weight_multiplier_38_p));
  Weight_Multiplier weight_multiplier_39 (.S(I_39), .W({8{1'b1}}), .P(weight_multiplier_39_p));
  Weight_Multiplier weight_multiplier_40 (.S(I_40), .W({8{1'b0}}), .P(weight_multiplier_40_p));
  Weight_Multiplier weight_multiplier_41 (.S(I_41), .W({8{1'b0}}), .P(weight_multiplier_41_p));
  Weight_Multiplier weight_multiplier_42 (.S(I_42), .W(8'hfc), .P(weight_multiplier_42_p));
  Weight_Multiplier weight_multiplier_43 (.S(I_43), .W(8'h3), .P(weight_multiplier_43_p));
  Weight_Multiplier weight_multiplier_44 (.S(I_44), .W(8'h1), .P(weight_multiplier_44_p));
  Weight_Multiplier weight_multiplier_45 (.S(I_45), .W({8{1'b1}}), .P(weight_multiplier_45_p));
  Weight_Multiplier weight_multiplier_46 (.S(I_46), .W(8'h1), .P(weight_multiplier_46_p));
  Weight_Multiplier weight_multiplier_47 (.S(I_47), .W(8'h2), .P(weight_multiplier_47_p));
  Weight_Multiplier weight_multiplier_48 (.S(I_48), .W({8{1'b0}}), .P(weight_multiplier_48_p));
  Weight_Multiplier weight_multiplier_49 (.S(I_49), .W({8{1'b1}}), .P(weight_multiplier_49_p));
  Weight_Multiplier weight_multiplier_50 (.S(I_50), .W(8'hfd), .P(weight_multiplier_50_p));
  Weight_Multiplier weight_multiplier_51 (.S(I_51), .W(8'h1), .P(weight_multiplier_51_p));
  Weight_Multiplier weight_multiplier_52 (.S(I_52), .W(8'h2), .P(weight_multiplier_52_p));
  Weight_Multiplier weight_multiplier_53 (.S(I_53), .W(8'hfe), .P(weight_multiplier_53_p));
  Weight_Multiplier weight_multiplier_54 (.S(I_54), .W(8'h3), .P(weight_multiplier_54_p));
  Weight_Multiplier weight_multiplier_55 (.S(I_55), .W(8'h2), .P(weight_multiplier_55_p));
  Weight_Multiplier weight_multiplier_56 (.S(I_56), .W(8'hfe), .P(weight_multiplier_56_p));
  Weight_Multiplier weight_multiplier_57 (.S(I_57), .W({8{1'b0}}), .P(weight_multiplier_57_p));
  Weight_Multiplier weight_multiplier_58 (.S(I_58), .W({8{1'b1}}), .P(weight_multiplier_58_p));
  Weight_Multiplier weight_multiplier_59 (.S(I_59), .W(8'hfe), .P(weight_multiplier_59_p));
  Weight_Multiplier weight_multiplier_60 (.S(I_60), .W({8{1'b1}}), .P(weight_multiplier_60_p));
  Weight_Multiplier weight_multiplier_61 (.S(I_61), .W(8'h1), .P(weight_multiplier_61_p));
  Weight_Multiplier weight_multiplier_62 (.S(I_62), .W(8'h2), .P(weight_multiplier_62_p));
  Weight_Multiplier weight_multiplier_63 (.S(I_63), .W({8{1'b0}}), .P(weight_multiplier_63_p));
  Weight_Multiplier weight_multiplier_64 (.S(I_64), .W(8'hfd), .P(weight_multiplier_64_p));
  Adder_Tree_8_Bit adder_tree_8_bit_1 (
    .A(weight_multiplier_1_p), .B(weight_multiplier_2_p), .C(weight_multiplier_3_p),
    .D(weight_multiplier_4_p), .E(weight_multiplier_5_p), .F(weight_multiplier_6_p),
    .G(weight_multiplier_7_p), .H(weight_multiplier_8_p), .S(adder_tree_8_bit_1_s));
  Adder_Tree_8_Bit adder_tree_8_bit_2 (
    .A(weight_multiplier_9_p), .B(weight_multiplier_10_p), .C(weight_multiplier_11_p),
    .D(weight_multiplier_12_p), .E(weight_multiplier_13_p), .F(weight_multiplier_14_p),
    .G(weight_multiplier_15_p), .H(weight_multiplier_16_p), .S(adder_tree_8_bit_2_s));
  Adder_Tree_8_Bit adder_tree_8_bit_3 (
    .A(weight_multiplier_17_p), .B(weight_multiplier_18_p), .C(weight_multiplier_19_p),
    .D(weight_multiplier_20_p), .E(weight_multiplier_21_p), .F(weight_multiplier_22_p),
    .G(weight_multiplier_23_p), .H(weight_multiplier_24_p), .S(adder_tree_8_bit_3_s));
  Adder_Tree_8_Bit adder_tree_8_bit_4 (
    .A(weight_multiplier_25_p), .B(weight_multiplier_26_p), .C(weight_multiplier_27_p),
    .D(weight_multiplier_28_p), .E(weight_multiplier_29_p), .F(weight_multiplier_30_p),
    .G(weight_multiplier_31_p), .H(weight_multiplier_32_p), .S(adder_tree_8_bit_4_s));
  Adder_Tree_8_Bit adder_tree_8_bit_5 (
    .A(weight_multiplier_33_p), .B(weight_multiplier_34_p), .C(weight_multiplier_35_p),
    .D(weight_multiplier_36_p), .E(weight_multiplier_37_p), .F(weight_multiplier_38_p),
    .G(weight_multiplier_39_p), .H(weight_multiplier_40_p), .S(adder_tree_8_bit_5_s));
  Adder_Tree_8_Bit adder_tree_8_bit_6 (
    .A(weight_multiplier_41_p), .B(weight_multiplier_42_p), .C(weight_multiplier_43_p),
    .D(weight_multiplier_44_p), .E(weight_multiplier_45_p), .F(weight_multiplier_46_p),
    .G(weight_multiplier_47_p), .H(weight_multiplier_48_p), .S(adder_tree_8_bit_6_s));
  Adder_Tree_8_Bit adder_tree_8_bit_7 (
    .A(weight_multiplier_49_p), .B(weight_multiplier_50_p), .C(weight_multiplier_51_p),
    .D(weight_multiplier_52_p), .E(weight_multiplier_53_p), .F(weight_multiplier_54_p),
    .G(weight_multiplier_55_p), .H(weight_multiplier_56_p), .S(adder_tree_8_bit_7_s));
  Adder_Tree_8_Bit adder_tree_8_bit_8 (
    .A(weight_multiplier_57_p), .B(weight_multiplier_58_p), .C(weight_multiplier_59_p),
    .D(weight_multiplier_60_p), .E(weight_multiplier_61_p), .F(weight_multiplier_62_p),
    .G(weight_multiplier_63_p), .H(weight_multiplier_64_p), .S(adder_tree_8_bit_8_s));
  Adder_Tree_8_Bit adder_tree_8_bit_9 (
    .A(adder_tree_8_bit_1_s), .B(adder_tree_8_bit_2_s), .C(adder_tree_8_bit_3_s), .D(adder_tree_8_bit_4_s),
    .E(adder_tree_8_bit_5_s), .F(adder_tree_8_bit_6_s), .G(adder_tree_8_bit_7_s), .H(adder_tree_8_bit_8_s),
    .S(adder_tree_8_bit_9_s));
  Adder_8_Bit_Bus adder_8_bit_bus_1 (.A(adder_tree_8_bit_9_s), .B(8'hfe), .Cin(1'b0), .S(Score_6));  // open: Cout
endmodule

module Perceptron_7 (
  input  I_1,
  input  I_2,
  input  I_3,
  input  I_4,
  input  I_5,
  input  I_6,
  input  I_7,
  input  I_8,
  input  I_9,
  input  I_10,
  input  I_11,
  input  I_12,
  input  I_13,
  input  I_14,
  input  I_15,
  input  I_16,
  input  I_17,
  input  I_18,
  input  I_19,
  input  I_20,
  input  I_21,
  input  I_22,
  input  I_23,
  input  I_24,
  input  I_25,
  input  I_26,
  input  I_27,
  input  I_28,
  input  I_29,
  input  I_30,
  input  I_31,
  input  I_32,
  input  I_33,
  input  I_34,
  input  I_35,
  input  I_36,
  input  I_37,
  input  I_38,
  input  I_39,
  input  I_40,
  input  I_41,
  input  I_42,
  input  I_43,
  input  I_44,
  input  I_45,
  input  I_46,
  input  I_47,
  input  I_48,
  input  I_49,
  input  I_50,
  input  I_51,
  input  I_52,
  input  I_53,
  input  I_54,
  input  I_55,
  input  I_56,
  input  I_57,
  input  I_58,
  input  I_59,
  input  I_60,
  input  I_61,
  input  I_62,
  input  I_63,
  input  I_64,
  output [7:0] Score_7
);

  wire [7:0] adder_tree_8_bit_1_s, adder_tree_8_bit_2_s, adder_tree_8_bit_3_s, adder_tree_8_bit_4_s,
       adder_tree_8_bit_5_s, adder_tree_8_bit_6_s, adder_tree_8_bit_7_s, adder_tree_8_bit_8_s,
       adder_tree_8_bit_9_s, weight_multiplier_1_p, weight_multiplier_2_p, weight_multiplier_3_p,
       weight_multiplier_4_p, weight_multiplier_5_p, weight_multiplier_6_p, weight_multiplier_7_p,
       weight_multiplier_8_p, weight_multiplier_9_p, weight_multiplier_10_p, weight_multiplier_11_p,
       weight_multiplier_12_p, weight_multiplier_13_p, weight_multiplier_14_p, weight_multiplier_15_p,
       weight_multiplier_16_p, weight_multiplier_17_p, weight_multiplier_18_p, weight_multiplier_19_p,
       weight_multiplier_20_p, weight_multiplier_21_p, weight_multiplier_22_p, weight_multiplier_23_p,
       weight_multiplier_24_p, weight_multiplier_25_p, weight_multiplier_26_p, weight_multiplier_27_p,
       weight_multiplier_28_p, weight_multiplier_29_p, weight_multiplier_30_p, weight_multiplier_31_p,
       weight_multiplier_32_p, weight_multiplier_33_p, weight_multiplier_34_p, weight_multiplier_35_p,
       weight_multiplier_36_p, weight_multiplier_37_p, weight_multiplier_38_p, weight_multiplier_39_p,
       weight_multiplier_40_p, weight_multiplier_41_p, weight_multiplier_42_p, weight_multiplier_43_p,
       weight_multiplier_44_p, weight_multiplier_45_p, weight_multiplier_46_p, weight_multiplier_47_p,
       weight_multiplier_48_p, weight_multiplier_49_p, weight_multiplier_50_p, weight_multiplier_51_p,
       weight_multiplier_52_p, weight_multiplier_53_p, weight_multiplier_54_p, weight_multiplier_55_p,
       weight_multiplier_56_p, weight_multiplier_57_p, weight_multiplier_58_p, weight_multiplier_59_p,
       weight_multiplier_60_p, weight_multiplier_61_p, weight_multiplier_62_p, weight_multiplier_63_p,
       weight_multiplier_64_p;

  Weight_Multiplier weight_multiplier_1 (.S(I_1), .W({8{1'b0}}), .P(weight_multiplier_1_p));
  Weight_Multiplier weight_multiplier_2 (.S(I_2), .W(8'hfe), .P(weight_multiplier_2_p));
  Weight_Multiplier weight_multiplier_3 (.S(I_3), .W({8{1'b0}}), .P(weight_multiplier_3_p));
  Weight_Multiplier weight_multiplier_4 (.S(I_4), .W(8'h2), .P(weight_multiplier_4_p));
  Weight_Multiplier weight_multiplier_5 (.S(I_5), .W(8'h1), .P(weight_multiplier_5_p));
  Weight_Multiplier weight_multiplier_6 (.S(I_6), .W(8'h1), .P(weight_multiplier_6_p));
  Weight_Multiplier weight_multiplier_7 (.S(I_7), .W(8'h2), .P(weight_multiplier_7_p));
  Weight_Multiplier weight_multiplier_8 (.S(I_8), .W(8'h1), .P(weight_multiplier_8_p));
  Weight_Multiplier weight_multiplier_9 (.S(I_9), .W({8{1'b0}}), .P(weight_multiplier_9_p));
  Weight_Multiplier weight_multiplier_10 (.S(I_10), .W(8'h1), .P(weight_multiplier_10_p));
  Weight_Multiplier weight_multiplier_11 (.S(I_11), .W(8'h1), .P(weight_multiplier_11_p));
  Weight_Multiplier weight_multiplier_12 (.S(I_12), .W(8'h1), .P(weight_multiplier_12_p));
  Weight_Multiplier weight_multiplier_13 (.S(I_13), .W(8'h3), .P(weight_multiplier_13_p));
  Weight_Multiplier weight_multiplier_14 (.S(I_14), .W({8{1'b0}}), .P(weight_multiplier_14_p));
  Weight_Multiplier weight_multiplier_15 (.S(I_15), .W(8'h1), .P(weight_multiplier_15_p));
  Weight_Multiplier weight_multiplier_16 (.S(I_16), .W(8'h3), .P(weight_multiplier_16_p));
  Weight_Multiplier weight_multiplier_17 (.S(I_17), .W({8{1'b0}}), .P(weight_multiplier_17_p));
  Weight_Multiplier weight_multiplier_18 (.S(I_18), .W(8'hfd), .P(weight_multiplier_18_p));
  Weight_Multiplier weight_multiplier_19 (.S(I_19), .W(8'hfe), .P(weight_multiplier_19_p));
  Weight_Multiplier weight_multiplier_20 (.S(I_20), .W(8'hfe), .P(weight_multiplier_20_p));
  Weight_Multiplier weight_multiplier_21 (.S(I_21), .W({8{1'b0}}), .P(weight_multiplier_21_p));
  Weight_Multiplier weight_multiplier_22 (.S(I_22), .W({8{1'b0}}), .P(weight_multiplier_22_p));
  Weight_Multiplier weight_multiplier_23 (.S(I_23), .W(8'h1), .P(weight_multiplier_23_p));
  Weight_Multiplier weight_multiplier_24 (.S(I_24), .W({8{1'b1}}), .P(weight_multiplier_24_p));
  Weight_Multiplier weight_multiplier_25 (.S(I_25), .W({8{1'b0}}), .P(weight_multiplier_25_p));
  Weight_Multiplier weight_multiplier_26 (.S(I_26), .W(8'hfc), .P(weight_multiplier_26_p));
  Weight_Multiplier weight_multiplier_27 (.S(I_27), .W({8{1'b0}}), .P(weight_multiplier_27_p));
  Weight_Multiplier weight_multiplier_28 (.S(I_28), .W(8'hfd), .P(weight_multiplier_28_p));
  Weight_Multiplier weight_multiplier_29 (.S(I_29), .W(8'h1), .P(weight_multiplier_29_p));
  Weight_Multiplier weight_multiplier_30 (.S(I_30), .W(8'h2), .P(weight_multiplier_30_p));
  Weight_Multiplier weight_multiplier_31 (.S(I_31), .W(8'h3), .P(weight_multiplier_31_p));
  Weight_Multiplier weight_multiplier_32 (.S(I_32), .W({8{1'b0}}), .P(weight_multiplier_32_p));
  Weight_Multiplier weight_multiplier_33 (.S(I_33), .W({8{1'b0}}), .P(weight_multiplier_33_p));
  Weight_Multiplier weight_multiplier_34 (.S(I_34), .W({8{1'b0}}), .P(weight_multiplier_34_p));
  Weight_Multiplier weight_multiplier_35 (.S(I_35), .W(8'h1), .P(weight_multiplier_35_p));
  Weight_Multiplier weight_multiplier_36 (.S(I_36), .W(8'h2), .P(weight_multiplier_36_p));
  Weight_Multiplier weight_multiplier_37 (.S(I_37), .W(8'h2), .P(weight_multiplier_37_p));
  Weight_Multiplier weight_multiplier_38 (.S(I_38), .W(8'h3), .P(weight_multiplier_38_p));
  Weight_Multiplier weight_multiplier_39 (.S(I_39), .W(8'h3), .P(weight_multiplier_39_p));
  Weight_Multiplier weight_multiplier_40 (.S(I_40), .W({8{1'b0}}), .P(weight_multiplier_40_p));
  Weight_Multiplier weight_multiplier_41 (.S(I_41), .W({8{1'b0}}), .P(weight_multiplier_41_p));
  Weight_Multiplier weight_multiplier_42 (.S(I_42), .W(8'h1), .P(weight_multiplier_42_p));
  Weight_Multiplier weight_multiplier_43 (.S(I_43), .W({8{1'b0}}), .P(weight_multiplier_43_p));
  Weight_Multiplier weight_multiplier_44 (.S(I_44), .W(8'h2), .P(weight_multiplier_44_p));
  Weight_Multiplier weight_multiplier_45 (.S(I_45), .W({8{1'b0}}), .P(weight_multiplier_45_p));
  Weight_Multiplier weight_multiplier_46 (.S(I_46), .W({8{1'b1}}), .P(weight_multiplier_46_p));
  Weight_Multiplier weight_multiplier_47 (.S(I_47), .W(8'hfe), .P(weight_multiplier_47_p));
  Weight_Multiplier weight_multiplier_48 (.S(I_48), .W({8{1'b0}}), .P(weight_multiplier_48_p));
  Weight_Multiplier weight_multiplier_49 (.S(I_49), .W({8{1'b1}}), .P(weight_multiplier_49_p));
  Weight_Multiplier weight_multiplier_50 (.S(I_50), .W(8'hfe), .P(weight_multiplier_50_p));
  Weight_Multiplier weight_multiplier_51 (.S(I_51), .W(8'hfe), .P(weight_multiplier_51_p));
  Weight_Multiplier weight_multiplier_52 (.S(I_52), .W(8'h2), .P(weight_multiplier_52_p));
  Weight_Multiplier weight_multiplier_53 (.S(I_53), .W(8'hfd), .P(weight_multiplier_53_p));
  Weight_Multiplier weight_multiplier_54 (.S(I_54), .W(8'hfd), .P(weight_multiplier_54_p));
  Weight_Multiplier weight_multiplier_55 (.S(I_55), .W({8{1'b1}}), .P(weight_multiplier_55_p));
  Weight_Multiplier weight_multiplier_56 (.S(I_56), .W({8{1'b1}}), .P(weight_multiplier_56_p));
  Weight_Multiplier weight_multiplier_57 (.S(I_57), .W({8{1'b0}}), .P(weight_multiplier_57_p));
  Weight_Multiplier weight_multiplier_58 (.S(I_58), .W({8{1'b1}}), .P(weight_multiplier_58_p));
  Weight_Multiplier weight_multiplier_59 (.S(I_59), .W({8{1'b0}}), .P(weight_multiplier_59_p));
  Weight_Multiplier weight_multiplier_60 (.S(I_60), .W(8'hfe), .P(weight_multiplier_60_p));
  Weight_Multiplier weight_multiplier_61 (.S(I_61), .W(8'hfe), .P(weight_multiplier_61_p));
  Weight_Multiplier weight_multiplier_62 (.S(I_62), .W(8'hfe), .P(weight_multiplier_62_p));
  Weight_Multiplier weight_multiplier_63 (.S(I_63), .W(8'hfe), .P(weight_multiplier_63_p));
  Weight_Multiplier weight_multiplier_64 (.S(I_64), .W(8'hfe), .P(weight_multiplier_64_p));
  Adder_Tree_8_Bit adder_tree_8_bit_1 (
    .A(weight_multiplier_1_p), .B(weight_multiplier_2_p), .C(weight_multiplier_3_p),
    .D(weight_multiplier_4_p), .E(weight_multiplier_5_p), .F(weight_multiplier_6_p),
    .G(weight_multiplier_7_p), .H(weight_multiplier_8_p), .S(adder_tree_8_bit_1_s));
  Adder_Tree_8_Bit adder_tree_8_bit_2 (
    .A(weight_multiplier_9_p), .B(weight_multiplier_10_p), .C(weight_multiplier_11_p),
    .D(weight_multiplier_12_p), .E(weight_multiplier_13_p), .F(weight_multiplier_14_p),
    .G(weight_multiplier_15_p), .H(weight_multiplier_16_p), .S(adder_tree_8_bit_2_s));
  Adder_Tree_8_Bit adder_tree_8_bit_3 (
    .A(weight_multiplier_17_p), .B(weight_multiplier_18_p), .C(weight_multiplier_19_p),
    .D(weight_multiplier_20_p), .E(weight_multiplier_21_p), .F(weight_multiplier_22_p),
    .G(weight_multiplier_23_p), .H(weight_multiplier_24_p), .S(adder_tree_8_bit_3_s));
  Adder_Tree_8_Bit adder_tree_8_bit_4 (
    .A(weight_multiplier_25_p), .B(weight_multiplier_26_p), .C(weight_multiplier_27_p),
    .D(weight_multiplier_28_p), .E(weight_multiplier_29_p), .F(weight_multiplier_30_p),
    .G(weight_multiplier_31_p), .H(weight_multiplier_32_p), .S(adder_tree_8_bit_4_s));
  Adder_Tree_8_Bit adder_tree_8_bit_5 (
    .A(weight_multiplier_33_p), .B(weight_multiplier_34_p), .C(weight_multiplier_35_p),
    .D(weight_multiplier_36_p), .E(weight_multiplier_37_p), .F(weight_multiplier_38_p),
    .G(weight_multiplier_39_p), .H(weight_multiplier_40_p), .S(adder_tree_8_bit_5_s));
  Adder_Tree_8_Bit adder_tree_8_bit_6 (
    .A(weight_multiplier_41_p), .B(weight_multiplier_42_p), .C(weight_multiplier_43_p),
    .D(weight_multiplier_44_p), .E(weight_multiplier_45_p), .F(weight_multiplier_46_p),
    .G(weight_multiplier_47_p), .H(weight_multiplier_48_p), .S(adder_tree_8_bit_6_s));
  Adder_Tree_8_Bit adder_tree_8_bit_7 (
    .A(weight_multiplier_49_p), .B(weight_multiplier_50_p), .C(weight_multiplier_51_p),
    .D(weight_multiplier_52_p), .E(weight_multiplier_53_p), .F(weight_multiplier_54_p),
    .G(weight_multiplier_55_p), .H(weight_multiplier_56_p), .S(adder_tree_8_bit_7_s));
  Adder_Tree_8_Bit adder_tree_8_bit_8 (
    .A(weight_multiplier_57_p), .B(weight_multiplier_58_p), .C(weight_multiplier_59_p),
    .D(weight_multiplier_60_p), .E(weight_multiplier_61_p), .F(weight_multiplier_62_p),
    .G(weight_multiplier_63_p), .H(weight_multiplier_64_p), .S(adder_tree_8_bit_8_s));
  Adder_Tree_8_Bit adder_tree_8_bit_9 (
    .A(adder_tree_8_bit_1_s), .B(adder_tree_8_bit_2_s), .C(adder_tree_8_bit_3_s), .D(adder_tree_8_bit_4_s),
    .E(adder_tree_8_bit_5_s), .F(adder_tree_8_bit_6_s), .G(adder_tree_8_bit_7_s), .H(adder_tree_8_bit_8_s),
    .S(adder_tree_8_bit_9_s));
  Adder_8_Bit_Bus adder_8_bit_bus_1 (.A(adder_tree_8_bit_9_s), .B({8{1'b0}}), .Cin(1'b0), .S(Score_7));  // open: Cout
endmodule
module Perceptron_8 (
  input  I_1,
  input  I_2,
  input  I_3,
  input  I_4,
  input  I_5,
  input  I_6,
  input  I_7,
  input  I_8,
  input  I_9,
  input  I_10,
  input  I_11,
  input  I_12,
  input  I_13,
  input  I_14,
  input  I_15,
  input  I_16,
  input  I_17,
  input  I_18,
  input  I_19,
  input  I_20,
  input  I_21,
  input  I_22,
  input  I_23,
  input  I_24,
  input  I_25,
  input  I_26,
  input  I_27,
  input  I_28,
  input  I_29,
  input  I_30,
  input  I_31,
  input  I_32,
  input  I_33,
  input  I_34,
  input  I_35,
  input  I_36,
  input  I_37,
  input  I_38,
  input  I_39,
  input  I_40,
  input  I_41,
  input  I_42,
  input  I_43,
  input  I_44,
  input  I_45,
  input  I_46,
  input  I_47,
  input  I_48,
  input  I_49,
  input  I_50,
  input  I_51,
  input  I_52,
  input  I_53,
  input  I_54,
  input  I_55,
  input  I_56,
  input  I_57,
  input  I_58,
  input  I_59,
  input  I_60,
  input  I_61,
  input  I_62,
  input  I_63,
  input  I_64,
  output [7:0] Score_8
);

  wire [7:0] adder_tree_8_bit_1_s, adder_tree_8_bit_2_s, adder_tree_8_bit_3_s, adder_tree_8_bit_4_s,
       adder_tree_8_bit_5_s, adder_tree_8_bit_6_s, adder_tree_8_bit_7_s, adder_tree_8_bit_8_s,
       adder_tree_8_bit_9_s, weight_multiplier_1_p, weight_multiplier_2_p, weight_multiplier_3_p,
       weight_multiplier_4_p, weight_multiplier_5_p, weight_multiplier_6_p, weight_multiplier_7_p,
       weight_multiplier_8_p, weight_multiplier_9_p, weight_multiplier_10_p, weight_multiplier_11_p,
       weight_multiplier_12_p, weight_multiplier_13_p, weight_multiplier_14_p, weight_multiplier_15_p,
       weight_multiplier_16_p, weight_multiplier_17_p, weight_multiplier_18_p, weight_multiplier_19_p,
       weight_multiplier_20_p, weight_multiplier_21_p, weight_multiplier_22_p, weight_multiplier_23_p,
       weight_multiplier_24_p, weight_multiplier_25_p, weight_multiplier_26_p, weight_multiplier_27_p,
       weight_multiplier_28_p, weight_multiplier_29_p, weight_multiplier_30_p, weight_multiplier_31_p,
       weight_multiplier_32_p, weight_multiplier_33_p, weight_multiplier_34_p, weight_multiplier_35_p,
       weight_multiplier_36_p, weight_multiplier_37_p, weight_multiplier_38_p, weight_multiplier_39_p,
       weight_multiplier_40_p, weight_multiplier_41_p, weight_multiplier_42_p, weight_multiplier_43_p,
       weight_multiplier_44_p, weight_multiplier_45_p, weight_multiplier_46_p, weight_multiplier_47_p,
       weight_multiplier_48_p, weight_multiplier_49_p, weight_multiplier_50_p, weight_multiplier_51_p,
       weight_multiplier_52_p, weight_multiplier_53_p, weight_multiplier_54_p, weight_multiplier_55_p,
       weight_multiplier_56_p, weight_multiplier_57_p, weight_multiplier_58_p, weight_multiplier_59_p,
       weight_multiplier_60_p, weight_multiplier_61_p, weight_multiplier_62_p, weight_multiplier_63_p,
       weight_multiplier_64_p;

  Weight_Multiplier weight_multiplier_1 (.S(I_1), .W({8{1'b0}}), .P(weight_multiplier_1_p));
  Weight_Multiplier weight_multiplier_2 (.S(I_2), .W(8'hfe), .P(weight_multiplier_2_p));
  Weight_Multiplier weight_multiplier_3 (.S(I_3), .W({8{1'b0}}), .P(weight_multiplier_3_p));
  Weight_Multiplier weight_multiplier_4 (.S(I_4), .W(8'h1), .P(weight_multiplier_4_p));
  Weight_Multiplier weight_multiplier_5 (.S(I_5), .W({8{1'b0}}), .P(weight_multiplier_5_p));
  Weight_Multiplier weight_multiplier_6 (.S(I_6), .W({8{1'b0}}), .P(weight_multiplier_6_p));
  Weight_Multiplier weight_multiplier_7 (.S(I_7), .W(8'hfc), .P(weight_multiplier_7_p));
  Weight_Multiplier weight_multiplier_8 (.S(I_8), .W({8{1'b1}}), .P(weight_multiplier_8_p));
  Weight_Multiplier weight_multiplier_9 (.S(I_9), .W({8{1'b0}}), .P(weight_multiplier_9_p));
  Weight_Multiplier weight_multiplier_10 (.S(I_10), .W({8{1'b1}}), .P(weight_multiplier_10_p));
  Weight_Multiplier weight_multiplier_11 (.S(I_11), .W(8'h1), .P(weight_multiplier_11_p));
  Weight_Multiplier weight_multiplier_12 (.S(I_12), .W({8{1'b0}}), .P(weight_multiplier_12_p));
  Weight_Multiplier weight_multiplier_13 (.S(I_13), .W(8'hfe), .P(weight_multiplier_13_p));
  Weight_Multiplier weight_multiplier_14 (.S(I_14), .W(8'h2), .P(weight_multiplier_14_p));
  Weight_Multiplier weight_multiplier_15 (.S(I_15), .W(8'h1), .P(weight_multiplier_15_p));
  Weight_Multiplier weight_multiplier_16 (.S(I_16), .W({8{1'b1}}), .P(weight_multiplier_16_p));
  Weight_Multiplier weight_multiplier_17 (.S(I_17), .W({8{1'b0}}), .P(weight_multiplier_17_p));
  Weight_Multiplier weight_multiplier_18 (.S(I_18), .W(8'h2), .P(weight_multiplier_18_p));
  Weight_Multiplier weight_multiplier_19 (.S(I_19), .W(8'h2), .P(weight_multiplier_19_p));
  Weight_Multiplier weight_multiplier_20 (.S(I_20), .W({8{1'b1}}), .P(weight_multiplier_20_p));
  Weight_Multiplier weight_multiplier_21 (.S(I_21), .W({8{1'b0}}), .P(weight_multiplier_21_p));
  Weight_Multiplier weight_multiplier_22 (.S(I_22), .W(8'h3), .P(weight_multiplier_22_p));
  Weight_Multiplier weight_multiplier_23 (.S(I_23), .W(8'h2), .P(weight_multiplier_23_p));
  Weight_Multiplier weight_multiplier_24 (.S(I_24), .W({8{1'b1}}), .P(weight_multiplier_24_p));
  Weight_Multiplier weight_multiplier_25 (.S(I_25), .W({8{1'b0}}), .P(weight_multiplier_25_p));
  Weight_Multiplier weight_multiplier_26 (.S(I_26), .W({8{1'b1}}), .P(weight_multiplier_26_p));
  Weight_Multiplier weight_multiplier_27 (.S(I_27), .W({8{1'b0}}), .P(weight_multiplier_27_p));
  Weight_Multiplier weight_multiplier_28 (.S(I_28), .W(8'h3), .P(weight_multiplier_28_p));
  Weight_Multiplier weight_multiplier_29 (.S(I_29), .W(8'h1), .P(weight_multiplier_29_p));
  Weight_Multiplier weight_multiplier_30 (.S(I_30), .W({8{1'b1}}), .P(weight_multiplier_30_p));
  Weight_Multiplier weight_multiplier_31 (.S(I_31), .W(8'hfe), .P(weight_multiplier_31_p));
  Weight_Multiplier weight_multiplier_32 (.S(I_32), .W({8{1'b0}}), .P(weight_multiplier_32_p));
  Weight_Multiplier weight_multiplier_33 (.S(I_33), .W({8{1'b0}}), .P(weight_multiplier_33_p));
  Weight_Multiplier weight_multiplier_34 (.S(I_34), .W({8{1'b1}}), .P(weight_multiplier_34_p));
  Weight_Multiplier weight_multiplier_35 (.S(I_35), .W({8{1'b0}}), .P(weight_multiplier_35_p));
  Weight_Multiplier weight_multiplier_36 (.S(I_36), .W(8'h4), .P(weight_multiplier_36_p));
  Weight_Multiplier weight_multiplier_37 (.S(I_37), .W({8{1'b0}}), .P(weight_multiplier_37_p));
  Weight_Multiplier weight_multiplier_38 (.S(I_38), .W(8'hfe), .P(weight_multiplier_38_p));
  Weight_Multiplier weight_multiplier_39 (.S(I_39), .W(8'hfd), .P(weight_multiplier_39_p));
  Weight_Multiplier weight_multiplier_40 (.S(I_40), .W({8{1'b0}}), .P(weight_multiplier_40_p));
  Weight_Multiplier weight_multiplier_41 (.S(I_41), .W({8{1'b0}}), .P(weight_multiplier_41_p));
  Weight_Multiplier weight_multiplier_42 (.S(I_42), .W(8'hfd), .P(weight_multiplier_42_p));
  Weight_Multiplier weight_multiplier_43 (.S(I_43), .W(8'h2), .P(weight_multiplier_43_p));
  Weight_Multiplier weight_multiplier_44 (.S(I_44), .W(8'h2), .P(weight_multiplier_44_p));
  Weight_Multiplier weight_multiplier_45 (.S(I_45), .W(8'h1), .P(weight_multiplier_45_p));
  Weight_Multiplier weight_multiplier_46 (.S(I_46), .W(8'h3), .P(weight_multiplier_46_p));
  Weight_Multiplier weight_multiplier_47 (.S(I_47), .W(8'hfe), .P(weight_multiplier_47_p));
  Weight_Multiplier weight_multiplier_48 (.S(I_48), .W({8{1'b0}}), .P(weight_multiplier_48_p));
  Weight_Multiplier weight_multiplier_49 (.S(I_49), .W({8{1'b1}}), .P(weight_multiplier_49_p));
  Weight_Multiplier weight_multiplier_50 (.S(I_50), .W(8'h3), .P(weight_multiplier_50_p));
  Weight_Multiplier weight_multiplier_51 (.S(I_51), .W(8'h2), .P(weight_multiplier_51_p));
  Weight_Multiplier weight_multiplier_52 (.S(I_52), .W(8'hfd), .P(weight_multiplier_52_p));
  Weight_Multiplier weight_multiplier_53 (.S(I_53), .W(8'hfe), .P(weight_multiplier_53_p));
  Weight_Multiplier weight_multiplier_54 (.S(I_54), .W(8'h2), .P(weight_multiplier_54_p));
  Weight_Multiplier weight_multiplier_55 (.S(I_55), .W({8{1'b0}}), .P(weight_multiplier_55_p));
  Weight_Multiplier weight_multiplier_56 (.S(I_56), .W(8'hfe), .P(weight_multiplier_56_p));
  Weight_Multiplier weight_multiplier_57 (.S(I_57), .W({8{1'b0}}), .P(weight_multiplier_57_p));
  Weight_Multiplier weight_multiplier_58 (.S(I_58), .W(8'hfe), .P(weight_multiplier_58_p));
  Weight_Multiplier weight_multiplier_59 (.S(I_59), .W(8'hfe), .P(weight_multiplier_59_p));
  Weight_Multiplier weight_multiplier_60 (.S(I_60), .W({8{1'b1}}), .P(weight_multiplier_60_p));
  Weight_Multiplier weight_multiplier_61 (.S(I_61), .W(8'h3), .P(weight_multiplier_61_p));
  Weight_Multiplier weight_multiplier_62 (.S(I_62), .W({8{1'b1}}), .P(weight_multiplier_62_p));
  Weight_Multiplier weight_multiplier_63 (.S(I_63), .W({8{1'b1}}), .P(weight_multiplier_63_p));
  Weight_Multiplier weight_multiplier_64 (.S(I_64), .W(8'hfe), .P(weight_multiplier_64_p));
  Adder_Tree_8_Bit adder_tree_8_bit_1 (
    .A(weight_multiplier_1_p), .B(weight_multiplier_2_p), .C(weight_multiplier_3_p),
    .D(weight_multiplier_4_p), .E(weight_multiplier_5_p), .F(weight_multiplier_6_p),
    .G(weight_multiplier_7_p), .H(weight_multiplier_8_p), .S(adder_tree_8_bit_1_s));
  Adder_Tree_8_Bit adder_tree_8_bit_2 (
    .A(weight_multiplier_9_p), .B(weight_multiplier_10_p), .C(weight_multiplier_11_p),
    .D(weight_multiplier_12_p), .E(weight_multiplier_13_p), .F(weight_multiplier_14_p),
    .G(weight_multiplier_15_p), .H(weight_multiplier_16_p), .S(adder_tree_8_bit_2_s));
  Adder_Tree_8_Bit adder_tree_8_bit_3 (
    .A(weight_multiplier_17_p), .B(weight_multiplier_18_p), .C(weight_multiplier_19_p),
    .D(weight_multiplier_20_p), .E(weight_multiplier_21_p), .F(weight_multiplier_22_p),
    .G(weight_multiplier_23_p), .H(weight_multiplier_24_p), .S(adder_tree_8_bit_3_s));
  Adder_Tree_8_Bit adder_tree_8_bit_4 (
    .A(weight_multiplier_25_p), .B(weight_multiplier_26_p), .C(weight_multiplier_27_p),
    .D(weight_multiplier_28_p), .E(weight_multiplier_29_p), .F(weight_multiplier_30_p),
    .G(weight_multiplier_31_p), .H(weight_multiplier_32_p), .S(adder_tree_8_bit_4_s));
  Adder_Tree_8_Bit adder_tree_8_bit_5 (
    .A(weight_multiplier_33_p), .B(weight_multiplier_34_p), .C(weight_multiplier_35_p),
    .D(weight_multiplier_36_p), .E(weight_multiplier_37_p), .F(weight_multiplier_38_p),
    .G(weight_multiplier_39_p), .H(weight_multiplier_40_p), .S(adder_tree_8_bit_5_s));
  Adder_Tree_8_Bit adder_tree_8_bit_6 (
    .A(weight_multiplier_41_p), .B(weight_multiplier_42_p), .C(weight_multiplier_43_p),
    .D(weight_multiplier_44_p), .E(weight_multiplier_45_p), .F(weight_multiplier_46_p),
    .G(weight_multiplier_47_p), .H(weight_multiplier_48_p), .S(adder_tree_8_bit_6_s));
  Adder_Tree_8_Bit adder_tree_8_bit_7 (
    .A(weight_multiplier_49_p), .B(weight_multiplier_50_p), .C(weight_multiplier_51_p),
    .D(weight_multiplier_52_p), .E(weight_multiplier_53_p), .F(weight_multiplier_54_p),
    .G(weight_multiplier_55_p), .H(weight_multiplier_56_p), .S(adder_tree_8_bit_7_s));
  Adder_Tree_8_Bit adder_tree_8_bit_8 (
    .A(weight_multiplier_57_p), .B(weight_multiplier_58_p), .C(weight_multiplier_59_p),
    .D(weight_multiplier_60_p), .E(weight_multiplier_61_p), .F(weight_multiplier_62_p),
    .G(weight_multiplier_63_p), .H(weight_multiplier_64_p), .S(adder_tree_8_bit_8_s));
  Adder_Tree_8_Bit adder_tree_8_bit_9 (
    .A(adder_tree_8_bit_1_s), .B(adder_tree_8_bit_2_s), .C(adder_tree_8_bit_3_s), .D(adder_tree_8_bit_4_s),
    .E(adder_tree_8_bit_5_s), .F(adder_tree_8_bit_6_s), .G(adder_tree_8_bit_7_s), .H(adder_tree_8_bit_8_s),
    .S(adder_tree_8_bit_9_s));
  Adder_8_Bit_Bus adder_8_bit_bus_1 (.A(adder_tree_8_bit_9_s), .B(8'hfd), .Cin(1'b0), .S(Score_8));  // open: Cout
endmodule

module Perceptron_9 (
  input  I_1,
  input  I_2,
  input  I_3,
  input  I_4,
  input  I_5,
  input  I_6,
  input  I_7,
  input  I_8,
  input  I_9,
  input  I_10,
  input  I_11,
  input  I_12,
  input  I_13,
  input  I_14,
  input  I_15,
  input  I_16,
  input  I_17,
  input  I_18,
  input  I_19,
  input  I_20,
  input  I_21,
  input  I_22,
  input  I_23,
  input  I_24,
  input  I_25,
  input  I_26,
  input  I_27,
  input  I_28,
  input  I_29,
  input  I_30,
  input  I_31,
  input  I_32,
  input  I_33,
  input  I_34,
  input  I_35,
  input  I_36,
  input  I_37,
  input  I_38,
  input  I_39,
  input  I_40,
  input  I_41,
  input  I_42,
  input  I_43,
  input  I_44,
  input  I_45,
  input  I_46,
  input  I_47,
  input  I_48,
  input  I_49,
  input  I_50,
  input  I_51,
  input  I_52,
  input  I_53,
  input  I_54,
  input  I_55,
  input  I_56,
  input  I_57,
  input  I_58,
  input  I_59,
  input  I_60,
  input  I_61,
  input  I_62,
  input  I_63,
  input  I_64,
  output [7:0] Score_9
);

  wire [7:0] adder_tree_8_bit_1_s, adder_tree_8_bit_2_s, adder_tree_8_bit_3_s, adder_tree_8_bit_4_s,
       adder_tree_8_bit_5_s, adder_tree_8_bit_6_s, adder_tree_8_bit_7_s, adder_tree_8_bit_8_s,
       adder_tree_8_bit_9_s, weight_multiplier_1_p, weight_multiplier_2_p, weight_multiplier_3_p,
       weight_multiplier_4_p, weight_multiplier_5_p, weight_multiplier_6_p, weight_multiplier_7_p,
       weight_multiplier_8_p, weight_multiplier_9_p, weight_multiplier_10_p, weight_multiplier_11_p,
       weight_multiplier_12_p, weight_multiplier_13_p, weight_multiplier_14_p, weight_multiplier_15_p,
       weight_multiplier_16_p, weight_multiplier_17_p, weight_multiplier_18_p, weight_multiplier_19_p,
       weight_multiplier_20_p, weight_multiplier_21_p, weight_multiplier_22_p, weight_multiplier_23_p,
       weight_multiplier_24_p, weight_multiplier_25_p, weight_multiplier_26_p, weight_multiplier_27_p,
       weight_multiplier_28_p, weight_multiplier_29_p, weight_multiplier_30_p, weight_multiplier_31_p,
       weight_multiplier_32_p, weight_multiplier_33_p, weight_multiplier_34_p, weight_multiplier_35_p,
       weight_multiplier_36_p, weight_multiplier_37_p, weight_multiplier_38_p, weight_multiplier_39_p,
       weight_multiplier_40_p, weight_multiplier_41_p, weight_multiplier_42_p, weight_multiplier_43_p,
       weight_multiplier_44_p, weight_multiplier_45_p, weight_multiplier_46_p, weight_multiplier_47_p,
       weight_multiplier_48_p, weight_multiplier_49_p, weight_multiplier_50_p, weight_multiplier_51_p,
       weight_multiplier_52_p, weight_multiplier_53_p, weight_multiplier_54_p, weight_multiplier_55_p,
       weight_multiplier_56_p, weight_multiplier_57_p, weight_multiplier_58_p, weight_multiplier_59_p,
       weight_multiplier_60_p, weight_multiplier_61_p, weight_multiplier_62_p, weight_multiplier_63_p,
       weight_multiplier_64_p;

  Weight_Multiplier weight_multiplier_1 (.S(I_1), .W({8{1'b0}}), .P(weight_multiplier_1_p));
  Weight_Multiplier weight_multiplier_2 (.S(I_2), .W(8'hfd), .P(weight_multiplier_2_p));
  Weight_Multiplier weight_multiplier_3 (.S(I_3), .W(8'h1), .P(weight_multiplier_3_p));
  Weight_Multiplier weight_multiplier_4 (.S(I_4), .W(8'h1), .P(weight_multiplier_4_p));
  Weight_Multiplier weight_multiplier_5 (.S(I_5), .W(8'h1), .P(weight_multiplier_5_p));
  Weight_Multiplier weight_multiplier_6 (.S(I_6), .W({8{1'b1}}), .P(weight_multiplier_6_p));
  Weight_Multiplier weight_multiplier_7 (.S(I_7), .W(8'h1), .P(weight_multiplier_7_p));
  Weight_Multiplier weight_multiplier_8 (.S(I_8), .W(8'hfe), .P(weight_multiplier_8_p));
  Weight_Multiplier weight_multiplier_9 (.S(I_9), .W({8{1'b0}}), .P(weight_multiplier_9_p));
  Weight_Multiplier weight_multiplier_10 (.S(I_10), .W({8{1'b0}}), .P(weight_multiplier_10_p));
  Weight_Multiplier weight_multiplier_11 (.S(I_11), .W(8'h2), .P(weight_multiplier_11_p));
  Weight_Multiplier weight_multiplier_12 (.S(I_12), .W({8{1'b0}}), .P(weight_multiplier_12_p));
  Weight_Multiplier weight_multiplier_13 (.S(I_13), .W({8{1'b0}}), .P(weight_multiplier_13_p));
  Weight_Multiplier weight_multiplier_14 (.S(I_14), .W(8'h1), .P(weight_multiplier_14_p));
  Weight_Multiplier weight_multiplier_15 (.S(I_15), .W(8'h1), .P(weight_multiplier_15_p));
  Weight_Multiplier weight_multiplier_16 (.S(I_16), .W(8'h1), .P(weight_multiplier_16_p));
  Weight_Multiplier weight_multiplier_17 (.S(I_17), .W({8{1'b0}}), .P(weight_multiplier_17_p));
  Weight_Multiplier weight_multiplier_18 (.S(I_18), .W(8'h2), .P(weight_multiplier_18_p));
  Weight_Multiplier weight_multiplier_19 (.S(I_19), .W(8'h3), .P(weight_multiplier_19_p));
  Weight_Multiplier weight_multiplier_20 (.S(I_20), .W({8{1'b0}}), .P(weight_multiplier_20_p));
  Weight_Multiplier weight_multiplier_21 (.S(I_21), .W({8{1'b0}}), .P(weight_multiplier_21_p));
  Weight_Multiplier weight_multiplier_22 (.S(I_22), .W(8'h4), .P(weight_multiplier_22_p));
  Weight_Multiplier weight_multiplier_23 (.S(I_23), .W(8'h1), .P(weight_multiplier_23_p));
  Weight_Multiplier weight_multiplier_24 (.S(I_24), .W(8'hfe), .P(weight_multiplier_24_p));
  Weight_Multiplier weight_multiplier_25 (.S(I_25), .W({8{1'b0}}), .P(weight_multiplier_25_p));
  Weight_Multiplier weight_multiplier_26 (.S(I_26), .W({8{1'b1}}), .P(weight_multiplier_26_p));
  Weight_Multiplier weight_multiplier_27 (.S(I_27), .W(8'h2), .P(weight_multiplier_27_p));
  Weight_Multiplier weight_multiplier_28 (.S(I_28), .W(8'h2), .P(weight_multiplier_28_p));
  Weight_Multiplier weight_multiplier_29 (.S(I_29), .W(8'h3), .P(weight_multiplier_29_p));
  Weight_Multiplier weight_multiplier_30 (.S(I_30), .W(8'h2), .P(weight_multiplier_30_p));
  Weight_Multiplier weight_multiplier_31 (.S(I_31), .W({8{1'b0}}), .P(weight_multiplier_31_p));
  Weight_Multiplier weight_multiplier_32 (.S(I_32), .W({8{1'b0}}), .P(weight_multiplier_32_p));
  Weight_Multiplier weight_multiplier_33 (.S(I_33), .W({8{1'b0}}), .P(weight_multiplier_33_p));
  Weight_Multiplier weight_multiplier_34 (.S(I_34), .W(8'hfd), .P(weight_multiplier_34_p));
  Weight_Multiplier weight_multiplier_35 (.S(I_35), .W({8{1'b1}}), .P(weight_multiplier_35_p));
  Weight_Multiplier weight_multiplier_36 (.S(I_36), .W({8{1'b0}}), .P(weight_multiplier_36_p));
  Weight_Multiplier weight_multiplier_37 (.S(I_37), .W(8'hfe), .P(weight_multiplier_37_p));
  Weight_Multiplier weight_multiplier_38 (.S(I_38), .W(8'h1), .P(weight_multiplier_38_p));
  Weight_Multiplier weight_multiplier_39 (.S(I_39), .W(8'h1), .P(weight_multiplier_39_p));
  Weight_Multiplier weight_multiplier_40 (.S(I_40), .W({8{1'b0}}), .P(weight_multiplier_40_p));
  Weight_Multiplier weight_multiplier_41 (.S(I_41), .W({8{1'b0}}), .P(weight_multiplier_41_p));
  Weight_Multiplier weight_multiplier_42 (.S(I_42), .W({8{1'b0}}), .P(weight_multiplier_42_p));
  Weight_Multiplier weight_multiplier_43 (.S(I_43), .W(8'hfd), .P(weight_multiplier_43_p));
  Weight_Multiplier weight_multiplier_44 (.S(I_44), .W(8'hfd), .P(weight_multiplier_44_p));
  Weight_Multiplier weight_multiplier_45 (.S(I_45), .W(8'hfe), .P(weight_multiplier_45_p));
  Weight_Multiplier weight_multiplier_46 (.S(I_46), .W({8{1'b0}}), .P(weight_multiplier_46_p));
  Weight_Multiplier weight_multiplier_47 (.S(I_47), .W({8{1'b1}}), .P(weight_multiplier_47_p));
  Weight_Multiplier weight_multiplier_48 (.S(I_48), .W({8{1'b0}}), .P(weight_multiplier_48_p));
  Weight_Multiplier weight_multiplier_49 (.S(I_49), .W({8{1'b1}}), .P(weight_multiplier_49_p));
  Weight_Multiplier weight_multiplier_50 (.S(I_50), .W(8'h3), .P(weight_multiplier_50_p));
  Weight_Multiplier weight_multiplier_51 (.S(I_51), .W(8'hfe), .P(weight_multiplier_51_p));
  Weight_Multiplier weight_multiplier_52 (.S(I_52), .W(8'hfd), .P(weight_multiplier_52_p));
  Weight_Multiplier weight_multiplier_53 (.S(I_53), .W(8'hfe), .P(weight_multiplier_53_p));
  Weight_Multiplier weight_multiplier_54 (.S(I_54), .W({8{1'b0}}), .P(weight_multiplier_54_p));
  Weight_Multiplier weight_multiplier_55 (.S(I_55), .W(8'h1), .P(weight_multiplier_55_p));
  Weight_Multiplier weight_multiplier_56 (.S(I_56), .W({8{1'b1}}), .P(weight_multiplier_56_p));
  Weight_Multiplier weight_multiplier_57 (.S(I_57), .W({8{1'b0}}), .P(weight_multiplier_57_p));
  Weight_Multiplier weight_multiplier_58 (.S(I_58), .W({8{1'b1}}), .P(weight_multiplier_58_p));
  Weight_Multiplier weight_multiplier_59 (.S(I_59), .W({8{1'b0}}), .P(weight_multiplier_59_p));
  Weight_Multiplier weight_multiplier_60 (.S(I_60), .W(8'h1), .P(weight_multiplier_60_p));
  Weight_Multiplier weight_multiplier_61 (.S(I_61), .W(8'h1), .P(weight_multiplier_61_p));
  Weight_Multiplier weight_multiplier_62 (.S(I_62), .W({8{1'b0}}), .P(weight_multiplier_62_p));
  Weight_Multiplier weight_multiplier_63 (.S(I_63), .W(8'hfe), .P(weight_multiplier_63_p));
  Weight_Multiplier weight_multiplier_64 (.S(I_64), .W(8'hfd), .P(weight_multiplier_64_p));
  Adder_Tree_8_Bit adder_tree_8_bit_1 (
    .A(weight_multiplier_1_p), .B(weight_multiplier_2_p), .C(weight_multiplier_3_p),
    .D(weight_multiplier_4_p), .E(weight_multiplier_5_p), .F(weight_multiplier_6_p),
    .G(weight_multiplier_7_p), .H(weight_multiplier_8_p), .S(adder_tree_8_bit_1_s));
  Adder_Tree_8_Bit adder_tree_8_bit_2 (
    .A(weight_multiplier_9_p), .B(weight_multiplier_10_p), .C(weight_multiplier_11_p),
    .D(weight_multiplier_12_p), .E(weight_multiplier_13_p), .F(weight_multiplier_14_p),
    .G(weight_multiplier_15_p), .H(weight_multiplier_16_p), .S(adder_tree_8_bit_2_s));
  Adder_Tree_8_Bit adder_tree_8_bit_3 (
    .A(weight_multiplier_17_p), .B(weight_multiplier_18_p), .C(weight_multiplier_19_p),
    .D(weight_multiplier_20_p), .E(weight_multiplier_21_p), .F(weight_multiplier_22_p),
    .G(weight_multiplier_23_p), .H(weight_multiplier_24_p), .S(adder_tree_8_bit_3_s));
  Adder_Tree_8_Bit adder_tree_8_bit_4 (
    .A(weight_multiplier_25_p), .B(weight_multiplier_26_p), .C(weight_multiplier_27_p),
    .D(weight_multiplier_28_p), .E(weight_multiplier_29_p), .F(weight_multiplier_30_p),
    .G(weight_multiplier_31_p), .H(weight_multiplier_32_p), .S(adder_tree_8_bit_4_s));
  Adder_Tree_8_Bit adder_tree_8_bit_5 (
    .A(weight_multiplier_33_p), .B(weight_multiplier_34_p), .C(weight_multiplier_35_p),
    .D(weight_multiplier_36_p), .E(weight_multiplier_37_p), .F(weight_multiplier_38_p),
    .G(weight_multiplier_39_p), .H(weight_multiplier_40_p), .S(adder_tree_8_bit_5_s));
  Adder_Tree_8_Bit adder_tree_8_bit_6 (
    .A(weight_multiplier_41_p), .B(weight_multiplier_42_p), .C(weight_multiplier_43_p),
    .D(weight_multiplier_44_p), .E(weight_multiplier_45_p), .F(weight_multiplier_46_p),
    .G(weight_multiplier_47_p), .H(weight_multiplier_48_p), .S(adder_tree_8_bit_6_s));
  Adder_Tree_8_Bit adder_tree_8_bit_7 (
    .A(weight_multiplier_49_p), .B(weight_multiplier_50_p), .C(weight_multiplier_51_p),
    .D(weight_multiplier_52_p), .E(weight_multiplier_53_p), .F(weight_multiplier_54_p),
    .G(weight_multiplier_55_p), .H(weight_multiplier_56_p), .S(adder_tree_8_bit_7_s));
  Adder_Tree_8_Bit adder_tree_8_bit_8 (
    .A(weight_multiplier_57_p), .B(weight_multiplier_58_p), .C(weight_multiplier_59_p),
    .D(weight_multiplier_60_p), .E(weight_multiplier_61_p), .F(weight_multiplier_62_p),
    .G(weight_multiplier_63_p), .H(weight_multiplier_64_p), .S(adder_tree_8_bit_8_s));
  Adder_Tree_8_Bit adder_tree_8_bit_9 (
    .A(adder_tree_8_bit_1_s), .B(adder_tree_8_bit_2_s), .C(adder_tree_8_bit_3_s), .D(adder_tree_8_bit_4_s),
    .E(adder_tree_8_bit_5_s), .F(adder_tree_8_bit_6_s), .G(adder_tree_8_bit_7_s), .H(adder_tree_8_bit_8_s),
    .S(adder_tree_8_bit_9_s));
  Adder_8_Bit_Bus adder_8_bit_bus_1 (.A(adder_tree_8_bit_9_s), .B({8{1'b0}}), .Cin(1'b0), .S(Score_9));  // open: Cout
endmodule

module Multiplexer_2_to_1_1Bit (
  input  D1,
  input  D0,
  input  S,
  output Y
);

  wire and_1_out, and_2_out, not_1_out;

  not not_1 (not_1_out, S);
  and and_1 (and_1_out, D1, S);
  and and_2 (and_2_out, D0, not_1_out);
  or or_1 (Y, and_1_out, and_2_out);
endmodule

module Multiplexer_2_to_1_2Bit (
  input  [1:0] D1,
  input  [1:0] D0,
  input  S,
  output [1:0] Y
);

  Multiplexer_2_to_1_1Bit multiplexer_2_to_1_1bit_1 (.D1(D1[1]), .D0(D0[1]), .S(S), .Y(Y[1]));
  Multiplexer_2_to_1_1Bit multiplexer_2_to_1_1bit_2 (.D1(D1[0]), .D0(D0[0]), .S(S), .Y(Y[0]));
endmodule

module Multiplexer_2_to_1_4Bit (
  input  [3:0] D1,
  input  [3:0] D0,
  input  S,
  output [3:0] Y
);

  Multiplexer_2_to_1_2Bit multiplexer_2_to_1_2bit_1 (.D1(D1[3:2]), .D0(D0[3:2]), .S(S), .Y(Y[3:2]));
  Multiplexer_2_to_1_2Bit multiplexer_2_to_1_2bit_2 (.D1(D1[1:0]), .D0(D0[1:0]), .S(S), .Y(Y[1:0]));
endmodule

module Multiplexer_2_to_1_8Bit (
  input  [7:0] D1,
  input  [7:0] D0,
  input  S,
  output [7:0] Y
);

  Multiplexer_2_to_1_4Bit multiplexer_2_to_1_4bit_1 (.D1(D1[7:4]), .D0(D0[7:4]), .S(S), .Y(Y[7:4]));
  Multiplexer_2_to_1_4Bit multiplexer_2_to_1_4bit_2 (.D1(D1[3:0]), .D0(D0[3:0]), .S(S), .Y(Y[3:0]));
endmodule

module Signed_Comparator_8Bit (
  input  [7:0] A,
  input  [7:0] B,
  output Is_A_G_E
);

  wire and_1_out, and_2_out, not_2_out, not_3_out, xnor_1_out;
  wire [7:0] adder_8_bit_bus_1_s, not_1_out;

  assign not_1_out = ~B;  // NOT_Gate not_1, 8 bits wide
  not not_2 (not_2_out, A[7]);
  Adder_8_Bit_Bus adder_8_bit_bus_1 (.A(A), .B(not_1_out), .Cin(1'b1), .S(adder_8_bit_bus_1_s));  // open: Cout
  xnor xnor_1 (xnor_1_out, B[7], A[7]);
  and and_1 (and_1_out, not_2_out, B[7]);
  not not_3 (not_3_out, adder_8_bit_bus_1_s[7]);
  and and_2 (and_2_out, not_3_out, xnor_1_out);
  or or_1 (Is_A_G_E, and_2_out, and_1_out);
endmodule

module Max_Forwarder (
  input  [7:0] Score_A,
  input  [7:0] Score_B,
  input  [3:0] ID_A,
  input  [3:0] ID_B,
  output [7:0] Max_Score,
  output [3:0] Max_ID
);

  wire signed_comparator_8bit_1_is_a_g_e;

  Signed_Comparator_8Bit signed_comparator_8bit_1 (
    .A(Score_A), .B(Score_B), .Is_A_G_E(signed_comparator_8bit_1_is_a_g_e));
  Multiplexer_2_to_1_8Bit multiplexer_2_to_1_8bit_1 (
    .D1(Score_A), .D0(Score_B), .S(signed_comparator_8bit_1_is_a_g_e), .Y(Max_Score));
  Multiplexer_2_to_1_4Bit multiplexer_2_to_1_4bit_1 (
    .D1(ID_A), .D0(ID_B), .S(signed_comparator_8bit_1_is_a_g_e), .Y(Max_ID));
endmodule

module Argmax_10_8Bit (
  input  [7:0] Score_0,
  input  [7:0] Score_1,
  input  [7:0] Score_2,
  input  [7:0] Score_3,
  input  [7:0] Score_4,
  input  [7:0] Score_5,
  input  [7:0] Score_6,
  input  [7:0] Score_7,
  input  [7:0] Score_8,
  input  [7:0] Score_9,
  output [3:0] Max_ID
);

  wire [3:0] max_forwarder_1_max_id, max_forwarder_2_max_id, max_forwarder_3_max_id, max_forwarder_4_max_id,
       max_forwarder_5_max_id, max_forwarder_6_max_id, max_forwarder_7_max_id, max_forwarder_8_max_id;
  wire [7:0] max_forwarder_1_max_score, max_forwarder_2_max_score, max_forwarder_3_max_score,
       max_forwarder_4_max_score, max_forwarder_5_max_score, max_forwarder_6_max_score,
       max_forwarder_7_max_score, max_forwarder_8_max_score;

  Max_Forwarder max_forwarder_1 (
    .Score_A(Score_0), .Score_B(Score_1), .ID_A(4'b0000), .ID_B(4'b0001),
    .Max_Score(max_forwarder_1_max_score), .Max_ID(max_forwarder_1_max_id));
  Max_Forwarder max_forwarder_2 (
    .Score_A(Score_2), .Score_B(Score_3), .ID_A(4'b0010), .ID_B(4'b0011),
    .Max_Score(max_forwarder_2_max_score), .Max_ID(max_forwarder_2_max_id));
  Max_Forwarder max_forwarder_3 (
    .Score_A(Score_4), .Score_B(Score_5), .ID_A(4'b0100), .ID_B(4'b0101),
    .Max_Score(max_forwarder_3_max_score), .Max_ID(max_forwarder_3_max_id));
  Max_Forwarder max_forwarder_4 (
    .Score_A(Score_6), .Score_B(Score_7), .ID_A(4'b0110), .ID_B(4'b0111),
    .Max_Score(max_forwarder_4_max_score), .Max_ID(max_forwarder_4_max_id));
  Max_Forwarder max_forwarder_5 (
    .Score_A(Score_8), .Score_B(Score_9), .ID_A(4'b1000), .ID_B(4'b1001),
    .Max_Score(max_forwarder_5_max_score), .Max_ID(max_forwarder_5_max_id));
  Max_Forwarder max_forwarder_6 (
    .Score_A(max_forwarder_1_max_score), .Score_B(max_forwarder_2_max_score), .ID_A(max_forwarder_1_max_id),
    .ID_B(max_forwarder_2_max_id), .Max_Score(max_forwarder_6_max_score), .Max_ID(max_forwarder_6_max_id));
  Max_Forwarder max_forwarder_7 (
    .Score_A(max_forwarder_3_max_score), .Score_B(max_forwarder_4_max_score), .ID_A(max_forwarder_3_max_id),
    .ID_B(max_forwarder_4_max_id), .Max_Score(max_forwarder_7_max_score), .Max_ID(max_forwarder_7_max_id));
  Max_Forwarder max_forwarder_8 (
    .Score_A(max_forwarder_6_max_score), .Score_B(max_forwarder_7_max_score), .ID_A(max_forwarder_6_max_id),
    .ID_B(max_forwarder_7_max_id), .Max_Score(max_forwarder_8_max_score), .Max_ID(max_forwarder_8_max_id));
  Max_Forwarder max_forwarder_9 (
    .Score_A(max_forwarder_8_max_score), .Score_B(max_forwarder_5_max_score), .ID_A(max_forwarder_8_max_id),
    .ID_B(max_forwarder_5_max_id), .Max_ID(Max_ID));  // open: Max_Score
endmodule

module Perceptron_0_Bus (
  input  [63:0] X,
  output [7:0] Score_0
);

  Perceptron_0 perceptron_0_1 (
    .I_1(X[63]), .I_2(X[62]), .I_3(X[61]), .I_4(X[60]), .I_5(X[59]), .I_6(X[58]), .I_7(X[57]), .I_8(X[56]),
    .I_9(X[55]), .I_10(X[54]), .I_11(X[53]), .I_12(X[52]), .I_13(X[51]), .I_14(X[50]), .I_15(X[49]),
    .I_16(X[48]), .I_17(X[47]), .I_18(X[46]), .I_19(X[45]), .I_20(X[44]), .I_21(X[43]), .I_22(X[42]),
    .I_23(X[41]), .I_24(X[40]), .I_25(X[39]), .I_26(X[38]), .I_27(X[37]), .I_28(X[36]), .I_29(X[35]),
    .I_30(X[34]), .I_31(X[33]), .I_32(X[32]), .I_33(X[31]), .I_34(X[30]), .I_35(X[29]), .I_36(X[28]),
    .I_37(X[27]), .I_38(X[26]), .I_39(X[25]), .I_40(X[24]), .I_41(X[23]), .I_42(X[22]), .I_43(X[21]),
    .I_44(X[20]), .I_45(X[19]), .I_46(X[18]), .I_47(X[17]), .I_48(X[16]), .I_49(X[15]), .I_50(X[14]),
    .I_51(X[13]), .I_52(X[12]), .I_53(X[11]), .I_54(X[10]), .I_55(X[9]), .I_56(X[8]), .I_57(X[7]),
    .I_58(X[6]), .I_59(X[5]), .I_60(X[4]), .I_61(X[3]), .I_62(X[2]), .I_63(X[1]), .I_64(X[0]),
    .Score_0(Score_0));
endmodule

module Perceptron_1_Bus (
  input  [63:0] X,
  output [7:0] Score_1
);

  Perceptron_1 perceptron_1_1 (
    .I_1(X[63]), .I_2(X[62]), .I_3(X[61]), .I_4(X[60]), .I_5(X[59]), .I_6(X[58]), .I_7(X[57]), .I_8(X[56]),
    .I_9(X[55]), .I_10(X[54]), .I_11(X[53]), .I_12(X[52]), .I_13(X[51]), .I_14(X[50]), .I_15(X[49]),
    .I_16(X[48]), .I_17(X[47]), .I_18(X[46]), .I_19(X[45]), .I_20(X[44]), .I_21(X[43]), .I_22(X[42]),
    .I_23(X[41]), .I_24(X[40]), .I_25(X[39]), .I_26(X[38]), .I_27(X[37]), .I_28(X[36]), .I_29(X[35]),
    .I_30(X[34]), .I_31(X[33]), .I_32(X[32]), .I_33(X[31]), .I_34(X[30]), .I_35(X[29]), .I_36(X[28]),
    .I_37(X[27]), .I_38(X[26]), .I_39(X[25]), .I_40(X[24]), .I_41(X[23]), .I_42(X[22]), .I_43(X[21]),
    .I_44(X[20]), .I_45(X[19]), .I_46(X[18]), .I_47(X[17]), .I_48(X[16]), .I_49(X[15]), .I_50(X[14]),
    .I_51(X[13]), .I_52(X[12]), .I_53(X[11]), .I_54(X[10]), .I_55(X[9]), .I_56(X[8]), .I_57(X[7]),
    .I_58(X[6]), .I_59(X[5]), .I_60(X[4]), .I_61(X[3]), .I_62(X[2]), .I_63(X[1]), .I_64(X[0]),
    .Score_1(Score_1));
endmodule

module Perceptron_2_Bus (
  input  [63:0] X,
  output [7:0] Score_2
);

  Perceptron_2 perceptron_2_1 (
    .I_1(X[63]), .I_2(X[62]), .I_3(X[61]), .I_4(X[60]), .I_5(X[59]), .I_6(X[58]), .I_7(X[57]), .I_8(X[56]),
    .I_9(X[55]), .I_10(X[54]), .I_11(X[53]), .I_12(X[52]), .I_13(X[51]), .I_14(X[50]), .I_15(X[49]),
    .I_16(X[48]), .I_17(X[47]), .I_18(X[46]), .I_19(X[45]), .I_20(X[44]), .I_21(X[43]), .I_22(X[42]),
    .I_23(X[41]), .I_24(X[40]), .I_25(X[39]), .I_26(X[38]), .I_27(X[37]), .I_28(X[36]), .I_29(X[35]),
    .I_30(X[34]), .I_31(X[33]), .I_32(X[32]), .I_33(X[31]), .I_34(X[30]), .I_35(X[29]), .I_36(X[28]),
    .I_37(X[27]), .I_38(X[26]), .I_39(X[25]), .I_40(X[24]), .I_41(X[23]), .I_42(X[22]), .I_43(X[21]),
    .I_44(X[20]), .I_45(X[19]), .I_46(X[18]), .I_47(X[17]), .I_48(X[16]), .I_49(X[15]), .I_50(X[14]),
    .I_51(X[13]), .I_52(X[12]), .I_53(X[11]), .I_54(X[10]), .I_55(X[9]), .I_56(X[8]), .I_57(X[7]),
    .I_58(X[6]), .I_59(X[5]), .I_60(X[4]), .I_61(X[3]), .I_62(X[2]), .I_63(X[1]), .I_64(X[0]),
    .Score_2(Score_2));
endmodule

module Perceptron_3_Bus (
  input  [63:0] X,
  output [7:0] Score_3
);

  Perceptron_3 perceptron_3_1 (
    .I_1(X[63]), .I_2(X[62]), .I_3(X[61]), .I_4(X[60]), .I_5(X[59]), .I_6(X[58]), .I_7(X[57]), .I_8(X[56]),
    .I_9(X[55]), .I_10(X[54]), .I_11(X[53]), .I_12(X[52]), .I_13(X[51]), .I_14(X[50]), .I_15(X[49]),
    .I_16(X[48]), .I_17(X[47]), .I_18(X[46]), .I_19(X[45]), .I_20(X[44]), .I_21(X[43]), .I_22(X[42]),
    .I_23(X[41]), .I_24(X[40]), .I_25(X[39]), .I_26(X[38]), .I_27(X[37]), .I_28(X[36]), .I_29(X[35]),
    .I_30(X[34]), .I_31(X[33]), .I_32(X[32]), .I_33(X[31]), .I_34(X[30]), .I_35(X[29]), .I_36(X[28]),
    .I_37(X[27]), .I_38(X[26]), .I_39(X[25]), .I_40(X[24]), .I_41(X[23]), .I_42(X[22]), .I_43(X[21]),
    .I_44(X[20]), .I_45(X[19]), .I_46(X[18]), .I_47(X[17]), .I_48(X[16]), .I_49(X[15]), .I_50(X[14]),
    .I_51(X[13]), .I_52(X[12]), .I_53(X[11]), .I_54(X[10]), .I_55(X[9]), .I_56(X[8]), .I_57(X[7]),
    .I_58(X[6]), .I_59(X[5]), .I_60(X[4]), .I_61(X[3]), .I_62(X[2]), .I_63(X[1]), .I_64(X[0]),
    .Score_3(Score_3));
endmodule

module Perceptron_4_Bus (
  input  [63:0] X,
  output [7:0] Score_4
);

  Perceptron_4 perceptron_4_1 (
    .I_1(X[63]), .I_2(X[62]), .I_3(X[61]), .I_4(X[60]), .I_5(X[59]), .I_6(X[58]), .I_7(X[57]), .I_8(X[56]),
    .I_9(X[55]), .I_10(X[54]), .I_11(X[53]), .I_12(X[52]), .I_13(X[51]), .I_14(X[50]), .I_15(X[49]),
    .I_16(X[48]), .I_17(X[47]), .I_18(X[46]), .I_19(X[45]), .I_20(X[44]), .I_21(X[43]), .I_22(X[42]),
    .I_23(X[41]), .I_24(X[40]), .I_25(X[39]), .I_26(X[38]), .I_27(X[37]), .I_28(X[36]), .I_29(X[35]),
    .I_30(X[34]), .I_31(X[33]), .I_32(X[32]), .I_33(X[31]), .I_34(X[30]), .I_35(X[29]), .I_36(X[28]),
    .I_37(X[27]), .I_38(X[26]), .I_39(X[25]), .I_40(X[24]), .I_41(X[23]), .I_42(X[22]), .I_43(X[21]),
    .I_44(X[20]), .I_45(X[19]), .I_46(X[18]), .I_47(X[17]), .I_48(X[16]), .I_49(X[15]), .I_50(X[14]),
    .I_51(X[13]), .I_52(X[12]), .I_53(X[11]), .I_54(X[10]), .I_55(X[9]), .I_56(X[8]), .I_57(X[7]),
    .I_58(X[6]), .I_59(X[5]), .I_60(X[4]), .I_61(X[3]), .I_62(X[2]), .I_63(X[1]), .I_64(X[0]),
    .Score_4(Score_4));
endmodule

module Perceptron_5_Bus (
  input  [63:0] X,
  output [7:0] Score_5
);

  Perceptron_5 perceptron_5_1 (
    .I_1(X[63]), .I_2(X[62]), .I_3(X[61]), .I_4(X[60]), .I_5(X[59]), .I_6(X[58]), .I_7(X[57]), .I_8(X[56]),
    .I_9(X[55]), .I_10(X[54]), .I_11(X[53]), .I_12(X[52]), .I_13(X[51]), .I_14(X[50]), .I_15(X[49]),
    .I_16(X[48]), .I_17(X[47]), .I_18(X[46]), .I_19(X[45]), .I_20(X[44]), .I_21(X[43]), .I_22(X[42]),
    .I_23(X[41]), .I_24(X[40]), .I_25(X[39]), .I_26(X[38]), .I_27(X[37]), .I_28(X[36]), .I_29(X[35]),
    .I_30(X[34]), .I_31(X[33]), .I_32(X[32]), .I_33(X[31]), .I_34(X[30]), .I_35(X[29]), .I_36(X[28]),
    .I_37(X[27]), .I_38(X[26]), .I_39(X[25]), .I_40(X[24]), .I_41(X[23]), .I_42(X[22]), .I_43(X[21]),
    .I_44(X[20]), .I_45(X[19]), .I_46(X[18]), .I_47(X[17]), .I_48(X[16]), .I_49(X[15]), .I_50(X[14]),
    .I_51(X[13]), .I_52(X[12]), .I_53(X[11]), .I_54(X[10]), .I_55(X[9]), .I_56(X[8]), .I_57(X[7]),
    .I_58(X[6]), .I_59(X[5]), .I_60(X[4]), .I_61(X[3]), .I_62(X[2]), .I_63(X[1]), .I_64(X[0]),
    .Score_5(Score_5));
endmodule

module Perceptron_6_Bus (
  input  [63:0] X,
  output [7:0] Score_6
);

  Perceptron_6 perceptron_6_1 (
    .I_1(X[63]), .I_2(X[62]), .I_3(X[61]), .I_4(X[60]), .I_5(X[59]), .I_6(X[58]), .I_7(X[57]), .I_8(X[56]),
    .I_9(X[55]), .I_10(X[54]), .I_11(X[53]), .I_12(X[52]), .I_13(X[51]), .I_14(X[50]), .I_15(X[49]),
    .I_16(X[48]), .I_17(X[47]), .I_18(X[46]), .I_19(X[45]), .I_20(X[44]), .I_21(X[43]), .I_22(X[42]),
    .I_23(X[41]), .I_24(X[40]), .I_25(X[39]), .I_26(X[38]), .I_27(X[37]), .I_28(X[36]), .I_29(X[35]),
    .I_30(X[34]), .I_31(X[33]), .I_32(X[32]), .I_33(X[31]), .I_34(X[30]), .I_35(X[29]), .I_36(X[28]),
    .I_37(X[27]), .I_38(X[26]), .I_39(X[25]), .I_40(X[24]), .I_41(X[23]), .I_42(X[22]), .I_43(X[21]),
    .I_44(X[20]), .I_45(X[19]), .I_46(X[18]), .I_47(X[17]), .I_48(X[16]), .I_49(X[15]), .I_50(X[14]),
    .I_51(X[13]), .I_52(X[12]), .I_53(X[11]), .I_54(X[10]), .I_55(X[9]), .I_56(X[8]), .I_57(X[7]),
    .I_58(X[6]), .I_59(X[5]), .I_60(X[4]), .I_61(X[3]), .I_62(X[2]), .I_63(X[1]), .I_64(X[0]),
    .Score_6(Score_6));
endmodule

module Perceptron_7_Bus (
  input  [63:0] X,
  output [7:0] Score_7
);

  Perceptron_7 perceptron_7_1 (
    .I_1(X[63]), .I_2(X[62]), .I_3(X[61]), .I_4(X[60]), .I_5(X[59]), .I_6(X[58]), .I_7(X[57]), .I_8(X[56]),
    .I_9(X[55]), .I_10(X[54]), .I_11(X[53]), .I_12(X[52]), .I_13(X[51]), .I_14(X[50]), .I_15(X[49]),
    .I_16(X[48]), .I_17(X[47]), .I_18(X[46]), .I_19(X[45]), .I_20(X[44]), .I_21(X[43]), .I_22(X[42]),
    .I_23(X[41]), .I_24(X[40]), .I_25(X[39]), .I_26(X[38]), .I_27(X[37]), .I_28(X[36]), .I_29(X[35]),
    .I_30(X[34]), .I_31(X[33]), .I_32(X[32]), .I_33(X[31]), .I_34(X[30]), .I_35(X[29]), .I_36(X[28]),
    .I_37(X[27]), .I_38(X[26]), .I_39(X[25]), .I_40(X[24]), .I_41(X[23]), .I_42(X[22]), .I_43(X[21]),
    .I_44(X[20]), .I_45(X[19]), .I_46(X[18]), .I_47(X[17]), .I_48(X[16]), .I_49(X[15]), .I_50(X[14]),
    .I_51(X[13]), .I_52(X[12]), .I_53(X[11]), .I_54(X[10]), .I_55(X[9]), .I_56(X[8]), .I_57(X[7]),
    .I_58(X[6]), .I_59(X[5]), .I_60(X[4]), .I_61(X[3]), .I_62(X[2]), .I_63(X[1]), .I_64(X[0]),
    .Score_7(Score_7));
endmodule

module Perceptron_8_Bus (
  input  [63:0] X,
  output [7:0] Score_8
);

  Perceptron_8 perceptron_8_1 (
    .I_1(X[63]), .I_2(X[62]), .I_3(X[61]), .I_4(X[60]), .I_5(X[59]), .I_6(X[58]), .I_7(X[57]), .I_8(X[56]),
    .I_9(X[55]), .I_10(X[54]), .I_11(X[53]), .I_12(X[52]), .I_13(X[51]), .I_14(X[50]), .I_15(X[49]),
    .I_16(X[48]), .I_17(X[47]), .I_18(X[46]), .I_19(X[45]), .I_20(X[44]), .I_21(X[43]), .I_22(X[42]),
    .I_23(X[41]), .I_24(X[40]), .I_25(X[39]), .I_26(X[38]), .I_27(X[37]), .I_28(X[36]), .I_29(X[35]),
    .I_30(X[34]), .I_31(X[33]), .I_32(X[32]), .I_33(X[31]), .I_34(X[30]), .I_35(X[29]), .I_36(X[28]),
    .I_37(X[27]), .I_38(X[26]), .I_39(X[25]), .I_40(X[24]), .I_41(X[23]), .I_42(X[22]), .I_43(X[21]),
    .I_44(X[20]), .I_45(X[19]), .I_46(X[18]), .I_47(X[17]), .I_48(X[16]), .I_49(X[15]), .I_50(X[14]),
    .I_51(X[13]), .I_52(X[12]), .I_53(X[11]), .I_54(X[10]), .I_55(X[9]), .I_56(X[8]), .I_57(X[7]),
    .I_58(X[6]), .I_59(X[5]), .I_60(X[4]), .I_61(X[3]), .I_62(X[2]), .I_63(X[1]), .I_64(X[0]),
    .Score_8(Score_8));
endmodule

module Perceptron_9_Bus (
  input  [63:0] X,
  output [7:0] Score_9
);

  Perceptron_9 perceptron_9_1 (
    .I_1(X[63]), .I_2(X[62]), .I_3(X[61]), .I_4(X[60]), .I_5(X[59]), .I_6(X[58]), .I_7(X[57]), .I_8(X[56]),
    .I_9(X[55]), .I_10(X[54]), .I_11(X[53]), .I_12(X[52]), .I_13(X[51]), .I_14(X[50]), .I_15(X[49]),
    .I_16(X[48]), .I_17(X[47]), .I_18(X[46]), .I_19(X[45]), .I_20(X[44]), .I_21(X[43]), .I_22(X[42]),
    .I_23(X[41]), .I_24(X[40]), .I_25(X[39]), .I_26(X[38]), .I_27(X[37]), .I_28(X[36]), .I_29(X[35]),
    .I_30(X[34]), .I_31(X[33]), .I_32(X[32]), .I_33(X[31]), .I_34(X[30]), .I_35(X[29]), .I_36(X[28]),
    .I_37(X[27]), .I_38(X[26]), .I_39(X[25]), .I_40(X[24]), .I_41(X[23]), .I_42(X[22]), .I_43(X[21]),
    .I_44(X[20]), .I_45(X[19]), .I_46(X[18]), .I_47(X[17]), .I_48(X[16]), .I_49(X[15]), .I_50(X[14]),
    .I_51(X[13]), .I_52(X[12]), .I_53(X[11]), .I_54(X[10]), .I_55(X[9]), .I_56(X[8]), .I_57(X[7]),
    .I_58(X[6]), .I_59(X[5]), .I_60(X[4]), .I_61(X[3]), .I_62(X[2]), .I_63(X[1]), .I_64(X[0]),
    .Score_9(Score_9));
endmodule

module Combined_Perceptron (
  input  I_1,
  input  I_2,
  input  I_3,
  input  I_4,
  input  I_5,
  input  I_6,
  input  I_7,
  input  I_8,
  input  I_9,
  input  I_10,
  input  I_11,
  input  I_12,
  input  I_13,
  input  I_14,
  input  I_15,
  input  I_16,
  input  I_17,
  input  I_18,
  input  I_19,
  input  I_20,
  input  I_21,
  input  I_22,
  input  I_23,
  input  I_24,
  input  I_25,
  input  I_26,
  input  I_27,
  input  I_28,
  input  I_29,
  input  I_30,
  input  I_31,
  input  I_32,
  input  I_33,
  input  I_34,
  input  I_35,
  input  I_36,
  input  I_37,
  input  I_38,
  input  I_39,
  input  I_40,
  input  I_41,
  input  I_42,
  input  I_43,
  input  I_44,
  input  I_45,
  input  I_46,
  input  I_47,
  input  I_48,
  input  I_49,
  input  I_50,
  input  I_51,
  input  I_52,
  input  I_53,
  input  I_54,
  input  I_55,
  input  I_56,
  input  I_57,
  input  I_58,
  input  I_59,
  input  I_60,
  input  I_61,
  input  I_62,
  input  I_63,
  input  I_64,
  output [3:0] Y
);

  wire [7:0] perceptron_0_bus_1_score_0, perceptron_1_bus_1_score_1, perceptron_2_bus_1_score_2,
       perceptron_3_bus_1_score_3, perceptron_4_bus_1_score_4, perceptron_5_bus_1_score_5,
       perceptron_6_bus_1_score_6, perceptron_7_bus_1_score_7, perceptron_8_bus_1_score_8,
       perceptron_9_bus_1_score_9;

  Perceptron_0_Bus perceptron_0_bus_1 (
    .X({I_1, I_2, I_3, I_4, I_5, I_6, I_7, I_8, I_9, I_10, I_11, I_12, I_13, I_14, I_15, I_16, I_17, I_18, I_19, I_20, I_21, I_22, I_23, I_24, I_25, I_26, I_27, I_28, I_29, I_30, I_31, I_32, I_33, I_34, I_35, I_36, I_37, I_38, I_39, I_40, I_41, I_42, I_43, I_44, I_45, I_46, I_47, I_48, I_49, I_50, I_51, I_52, I_53, I_54, I_55, I_56, I_57, I_58, I_59, I_60, I_61, I_62, I_63, I_64}),
    .Score_0(perceptron_0_bus_1_score_0));
  Perceptron_1_Bus perceptron_1_bus_1 (
    .X({I_1, I_2, I_3, I_4, I_5, I_6, I_7, I_8, I_9, I_10, I_11, I_12, I_13, I_14, I_15, I_16, I_17, I_18, I_19, I_20, I_21, I_22, I_23, I_24, I_25, I_26, I_27, I_28, I_29, I_30, I_31, I_32, I_33, I_34, I_35, I_36, I_37, I_38, I_39, I_40, I_41, I_42, I_43, I_44, I_45, I_46, I_47, I_48, I_49, I_50, I_51, I_52, I_53, I_54, I_55, I_56, I_57, I_58, I_59, I_60, I_61, I_62, I_63, I_64}),
    .Score_1(perceptron_1_bus_1_score_1));
  Perceptron_2_Bus perceptron_2_bus_1 (
    .X({I_1, I_2, I_3, I_4, I_5, I_6, I_7, I_8, I_9, I_10, I_11, I_12, I_13, I_14, I_15, I_16, I_17, I_18, I_19, I_20, I_21, I_22, I_23, I_24, I_25, I_26, I_27, I_28, I_29, I_30, I_31, I_32, I_33, I_34, I_35, I_36, I_37, I_38, I_39, I_40, I_41, I_42, I_43, I_44, I_45, I_46, I_47, I_48, I_49, I_50, I_51, I_52, I_53, I_54, I_55, I_56, I_57, I_58, I_59, I_60, I_61, I_62, I_63, I_64}),
    .Score_2(perceptron_2_bus_1_score_2));
  Perceptron_3_Bus perceptron_3_bus_1 (
    .X({I_1, I_2, I_3, I_4, I_5, I_6, I_7, I_8, I_9, I_10, I_11, I_12, I_13, I_14, I_15, I_16, I_17, I_18, I_19, I_20, I_21, I_22, I_23, I_24, I_25, I_26, I_27, I_28, I_29, I_30, I_31, I_32, I_33, I_34, I_35, I_36, I_37, I_38, I_39, I_40, I_41, I_42, I_43, I_44, I_45, I_46, I_47, I_48, I_49, I_50, I_51, I_52, I_53, I_54, I_55, I_56, I_57, I_58, I_59, I_60, I_61, I_62, I_63, I_64}),
    .Score_3(perceptron_3_bus_1_score_3));
  Perceptron_4_Bus perceptron_4_bus_1 (
    .X({I_1, I_2, I_3, I_4, I_5, I_6, I_7, I_8, I_9, I_10, I_11, I_12, I_13, I_14, I_15, I_16, I_17, I_18, I_19, I_20, I_21, I_22, I_23, I_24, I_25, I_26, I_27, I_28, I_29, I_30, I_31, I_32, I_33, I_34, I_35, I_36, I_37, I_38, I_39, I_40, I_41, I_42, I_43, I_44, I_45, I_46, I_47, I_48, I_49, I_50, I_51, I_52, I_53, I_54, I_55, I_56, I_57, I_58, I_59, I_60, I_61, I_62, I_63, I_64}),
    .Score_4(perceptron_4_bus_1_score_4));
  Perceptron_5_Bus perceptron_5_bus_1 (
    .X({I_1, I_2, I_3, I_4, I_5, I_6, I_7, I_8, I_9, I_10, I_11, I_12, I_13, I_14, I_15, I_16, I_17, I_18, I_19, I_20, I_21, I_22, I_23, I_24, I_25, I_26, I_27, I_28, I_29, I_30, I_31, I_32, I_33, I_34, I_35, I_36, I_37, I_38, I_39, I_40, I_41, I_42, I_43, I_44, I_45, I_46, I_47, I_48, I_49, I_50, I_51, I_52, I_53, I_54, I_55, I_56, I_57, I_58, I_59, I_60, I_61, I_62, I_63, I_64}),
    .Score_5(perceptron_5_bus_1_score_5));
  Perceptron_6_Bus perceptron_6_bus_1 (
    .X({I_1, I_2, I_3, I_4, I_5, I_6, I_7, I_8, I_9, I_10, I_11, I_12, I_13, I_14, I_15, I_16, I_17, I_18, I_19, I_20, I_21, I_22, I_23, I_24, I_25, I_26, I_27, I_28, I_29, I_30, I_31, I_32, I_33, I_34, I_35, I_36, I_37, I_38, I_39, I_40, I_41, I_42, I_43, I_44, I_45, I_46, I_47, I_48, I_49, I_50, I_51, I_52, I_53, I_54, I_55, I_56, I_57, I_58, I_59, I_60, I_61, I_62, I_63, I_64}),
    .Score_6(perceptron_6_bus_1_score_6));
  Perceptron_7_Bus perceptron_7_bus_1 (
    .X({I_1, I_2, I_3, I_4, I_5, I_6, I_7, I_8, I_9, I_10, I_11, I_12, I_13, I_14, I_15, I_16, I_17, I_18, I_19, I_20, I_21, I_22, I_23, I_24, I_25, I_26, I_27, I_28, I_29, I_30, I_31, I_32, I_33, I_34, I_35, I_36, I_37, I_38, I_39, I_40, I_41, I_42, I_43, I_44, I_45, I_46, I_47, I_48, I_49, I_50, I_51, I_52, I_53, I_54, I_55, I_56, I_57, I_58, I_59, I_60, I_61, I_62, I_63, I_64}),
    .Score_7(perceptron_7_bus_1_score_7));
  Perceptron_8_Bus perceptron_8_bus_1 (
    .X({I_1, I_2, I_3, I_4, I_5, I_6, I_7, I_8, I_9, I_10, I_11, I_12, I_13, I_14, I_15, I_16, I_17, I_18, I_19, I_20, I_21, I_22, I_23, I_24, I_25, I_26, I_27, I_28, I_29, I_30, I_31, I_32, I_33, I_34, I_35, I_36, I_37, I_38, I_39, I_40, I_41, I_42, I_43, I_44, I_45, I_46, I_47, I_48, I_49, I_50, I_51, I_52, I_53, I_54, I_55, I_56, I_57, I_58, I_59, I_60, I_61, I_62, I_63, I_64}),
    .Score_8(perceptron_8_bus_1_score_8));
  Perceptron_9_Bus perceptron_9_bus_1 (
    .X({I_1, I_2, I_3, I_4, I_5, I_6, I_7, I_8, I_9, I_10, I_11, I_12, I_13, I_14, I_15, I_16, I_17, I_18, I_19, I_20, I_21, I_22, I_23, I_24, I_25, I_26, I_27, I_28, I_29, I_30, I_31, I_32, I_33, I_34, I_35, I_36, I_37, I_38, I_39, I_40, I_41, I_42, I_43, I_44, I_45, I_46, I_47, I_48, I_49, I_50, I_51, I_52, I_53, I_54, I_55, I_56, I_57, I_58, I_59, I_60, I_61, I_62, I_63, I_64}),
    .Score_9(perceptron_9_bus_1_score_9));
  Argmax_10_8Bit argmax_10_8bit_1 (
    .Score_0(perceptron_0_bus_1_score_0), .Score_1(perceptron_1_bus_1_score_1),
    .Score_2(perceptron_2_bus_1_score_2), .Score_3(perceptron_3_bus_1_score_3),
    .Score_4(perceptron_4_bus_1_score_4), .Score_5(perceptron_5_bus_1_score_5),
    .Score_6(perceptron_6_bus_1_score_6), .Score_7(perceptron_7_bus_1_score_7),
    .Score_8(perceptron_8_bus_1_score_8), .Score_9(perceptron_9_bus_1_score_9), .Max_ID(Y));
endmodule
